// Logisim project PC_DOCS.circ as structural Verilog: 1 circuit, main circuit ProgramCounter
module ProgramCounter (
  input  [31:0] TargetAddr,
  input  BranchCtl,
  input  PCWEn,
  input  Clk,
  input  Reset,
  output [31:0] PcOut,
  output [31:0] PcPlus4
);

  wire [31:0] multiplexer_1_out;

  Multiplexer #(.width(32)) multiplexer_1 (.in0(PcPlus4), .in1(TargetAddr), .out(multiplexer_1_out), .sel(BranchCtl));
  Register #(.width(32)) register_1 (.D(multiplexer_1_out), .en(PCWEn), .clk(Clk), .Q(PcOut), .clr(Reset));
  Adder #(.width(32)) adder_1 (.a(32'h4), .b(PcOut), .out(PcPlus4));  // open: cin, cout
endmodule
