// Logisim project RiskVALU.circ as structural Verilog: 5 circuits, main circuit ALUControl
module ALUBase (
  input  [31:0] dataA,
  input  [31:0] dataB,
  input  [3:0] sel,
  output [31:0] Out0
);

  wire comparator_1_lt, comparator_2_lt;
  wire [31:0] add_t, and_t, or_t, sll_t, slt_t, sltu_t, sra_t, srl_t, sub_t, xor_t;

  Adder #(.width(32)) adder_1 (.a(dataA), .b(dataB), .out(add_t));  // open: cin, cout
  Subtractor #(.width(32)) subtractor_1 (.a(dataA), .b(dataB), .out(sub_t));  // open: bin, bout
  Shifter #(.width(32)) shifter_1 (.in(dataA), .\dist (dataB[4:0]), .out(sll_t));
  Shifter #(.shift("lr"), .width(32)) shifter_2 (.in(dataA), .\dist (dataB[4:0]), .out(srl_t));
  Shifter #(.shift("ar"), .width(32)) shifter_3 (.in(dataA), .\dist (dataB[4:0]), .out(sra_t));
  assign and_t = dataA & dataB;  // AND_Gate and_1, 32 bits wide
  assign or_t = dataA | dataB;  // OR_Gate or_1, 32 bits wide
  assign xor_t = dataA ^ dataB;  // XOR_Gate xor_1, 32 bits wide
  Comparator #(.width(32)) comparator_1 (.a(dataA), .b(dataB), .lt(comparator_1_lt));  // open: gt, eq
  Comparator #(.width(32)) comparator_2 (.a(dataA), .b(dataB), .lt(comparator_2_lt));  // open: gt, eq
  assign slt_t = {{31{1'b0}}, comparator_1_lt};  // Bit_Extender bit_extender_1
  assign sltu_t = {{31{1'b0}}, comparator_2_lt};  // Bit_Extender bit_extender_2
  Multiplexer #(.select(4), .width(32)) multiplexer_1 (
    .in0(add_t), .in1(sll_t), .in2(slt_t), .in3(sltu_t), .in4(xor_t), .in5(srl_t), .in6(or_t), .in7(and_t),
    .in8(sub_t), .in13(sra_t), .out(Out0), .sel(sel));  // open: in9, in10, in11, in12, in14, in15
  // Probe on sel

  // Other names for the same wires on the sheet: shamt[4:0] = dataB[4:0]

  // Notes on the sheet:
  //   sel[3] = func7[5]
  //   sel[2:0] = func3
  //   Select control
  //   Select control
  //   add = 0000
  //   sll = 0001
  //   slt = 0010
  //   sltu = 0011
  //   xor = 0100
  //   srl = 0101
  //   or = 0110
  //   and = 0111
  //   sub = 1000
  //   sra = 1101
endmodule

module ALUDataSource (
  input  [31:0] RDataA,
  input  [31:0] PC,
  input  ASel,
  input  [31:0] RDataB,
  input  [31:0] ImmVal,
  input  BSel,
  output [31:0] DataA,
  output [31:0] DataB
);

  Multiplexer #(.width(32)) multiplexer_1 (.in0(RDataA), .in1(PC), .out(DataA), .sel(ASel));
  Multiplexer #(.width(32)) multiplexer_2 (.in0(RDataB), .in1(ImmVal), .out(DataB), .sel(BSel));
endmodule

module ALUControl (
  input  [31:0] RDataA,
  input  [31:0] PC,
  input  ASel,
  input  [31:0] RDataB,
  input  [31:0] ImmVal,
  input  BSel,
  input  [4:0] ALUSel,
  output [31:0] Out0
);

  wire [31:0] baseOut, dataA, dataB, mulDivOut;

  ALUDataSource aludatasource_1 (
    .RDataA(RDataA), .PC(PC), .ASel(ASel), .RDataB(RDataB), .ImmVal(ImmVal), .BSel(BSel), .DataA(dataA),
    .DataB(dataB));
  // Probe on dataA
  // Probe on dataB
  // Probe on ALUSel[2:0]
  // Probe on ALUSel[3:0]
  ALUMulDiv alumuldiv_1 (.dataA(dataA), .dataB(dataB), .sel(ALUSel[2:0]), .OutData(mulDivOut));
  ALUBase alubase_1 (.dataA(dataA), .dataB(dataB), .sel(ALUSel[3:0]), .Out0(baseOut));
  // Probe on baseOut
  // Probe on mulDivOut
  Multiplexer #(.select(2), .width(32)) multiplexer_1 (
    .in0(baseOut), .in1(baseOut), .in2(mulDivOut), .out(Out0), .sel(ALUSel[4:3]));  // open: in3
  // Probe on Out0
  // Probe on ALUSel[4:3]

  // Other names for the same wires on the sheet: sel[4:0] = ALUSel

  // Notes on the sheet:
  //   sel[4:3] = func7[0] func7[5]
  //   sel[2:0] = func3
  //   Select control
endmodule

module ALUMulDiv (
  input  [31:0] dataA,
  input  [31:0] dataB,
  input  [2:0] sel,
  output [31:0] OutData
);

  wire and_4_out, and_5_out, divSign, signedDiv;
  wire [31:0] and_2_out, and_3_out, and_6_out, and_7_out, data_a_pre_div, data_b_pre_div, div, divOut,
       divSignExt, mul, mul_h_out, mulh, mulhsu, rem_t, remOut, remSignExt, signAExt, signBExt, signDivExt,
       xor_1_out, xor_2_out, xor_3_out, xor_4_out, xor_6_out, xor_7_out;

  // Probe on OutData
  // Probe on OutData
  // Probe on OutData
  and and_1 (signedDiv, ~sel[0], sel[2]);  // AND_Gate
  assign and_2_out = signDivExt & signBExt;  // AND_Gate and_2, 32 bits wide
  assign signAExt = {{31{dataA[31]}}, dataA[31]};  // Bit_Extender bit_extender_1
  assign signBExt = {{31{dataB[31]}}, dataB[31]};  // Bit_Extender bit_extender_2
  assign signDivExt = {{31{signedDiv}}, signedDiv};  // Bit_Extender bit_extender_3
  assign and_3_out = signDivExt & signAExt;  // AND_Gate and_3, 32 bits wide
  assign xor_1_out = dataA ^ and_3_out;  // XOR_Gate xor_1, 32 bits wide
  assign xor_2_out = dataB ^ and_2_out;  // XOR_Gate xor_2, 32 bits wide
  and and_4 (and_4_out, dataA[31], signedDiv);
  Adder #(.width(32)) adder_1 (.a(xor_1_out), .b({32{1'b0}}), .out(data_a_pre_div), .cin(and_4_out));  // open: cout
  and and_5 (and_5_out, dataB[31], signedDiv);
  Adder #(.width(32)) adder_2 (.a(xor_2_out), .b({32{1'b0}}), .out(data_b_pre_div), .cin(and_5_out));  // open: cout
  // Probe on dataA
  // Probe on dataB
  // Probe on data_a_pre_div
  // Probe on data_b_pre_div
  // Probe on mul_h_out
  // Probe on mul
  Multiplier #(.width(32)) multiplier_1 (.a(dataA), .b(dataB), .out(mul), .cout(mul_h_out));  // open: cin
  // Probe on divOut
  Divider #(.width(32)) divider_1 (.a(data_a_pre_div), .b(data_b_pre_div), .out(divOut), .rem(remOut));  // open: upper
  // Probe on remOut
  assign xor_3_out = dataB ^ signAExt;  // XOR_Gate xor_3, 32 bits wide
  assign xor_4_out = dataA ^ signBExt;  // XOR_Gate xor_4, 32 bits wide
  xor xor_5 (divSign, dataA[31], dataB[31]);
  assign divSignExt = {{31{divSign}}, divSign};  // Bit_Extender bit_extender_4
  assign remSignExt = {{31{dataA[31]}}, dataA[31]};  // Bit_Extender bit_extender_5
  assign and_6_out = signAExt & xor_3_out;  // AND_Gate and_6, 32 bits wide
  assign and_7_out = signBExt & xor_4_out;  // AND_Gate and_7, 32 bits wide
  Adder #(.width(32)) adder_3 (.a(mul_h_out), .b(and_6_out), .out(mulhsu), .cin(dataA[31]));  // open: cout
  Adder #(.width(32)) adder_4 (.a(mulhsu), .b(and_7_out), .out(mulh), .cin(dataB[31]));  // open: cout
  // Probe on mulhsu
  // Probe on mulh
  assign xor_6_out = divOut ^ divSignExt;  // XOR_Gate xor_6, 32 bits wide
  assign xor_7_out = remOut ^ remSignExt;  // XOR_Gate xor_7, 32 bits wide
  Adder #(.width(32)) adder_5 (.a(xor_6_out), .b({32{1'b0}}), .out(div), .cin(divSign));  // open: cout
  Adder #(.width(32)) adder_6 (.a(xor_7_out), .b({32{1'b0}}), .out(rem_t), .cin(dataA[31]));  // open: cout
  // Probe on mul
  // Probe on mulh
  // Probe on mulhsu
  // Probe on mul_h_out
  // Probe on div
  // Probe on rem_t
  // Probe on divOut
  // Probe on remOut
  // Probe on OutData
  Multiplexer #(.select(3), .width(32)) multiplexer_1 (
    .in0(mul), .in1(mulh), .in2(mulhsu), .in3(mul_h_out), .in4(div), .in5(divOut), .in6(rem_t), .in7(remOut),
    .out(OutData), .sel(sel));

  // Other names for the same wires on the sheet: remSign = dataA[31]; signA = dataA[31]; signB = dataB[31];
  //   divSigned[31:0] = div; divu[31:0] = divOut; mul_out[31:0] = mul; mulhu[31:0] = mul_h_out;
  //   remSigned[31:0] = rem_t; remu[31:0] = remOut; sub_a_out[31:0] = mulh; sub_b_out[31:0] = mulhsu

  // Notes on the sheet:
  //   mul = 000
  //   mulh = 001
  //   mulhsu = 010
  //   mulhu = 011
  //   div = 100
  //   divu = 101
  //   rem = 110
  //   remu = 111
  //   Select control
  //   sel[2:0] = func3
  //   Select control
  //   unsigned
  //   signed
  //   hex
  //   Multiply Signals
  //   Divide Signals
  //   Divide Pre-Process
  //   Multiply
  //   Divide
  //   Multiply Post Process
  //   Divide Post Process
  //   No corrections
  //   Apply both corrections
  //   Only apply B correction
  //   No corrections
  //   Multiply Output
  //   Divide Output
  //   mul = 000
  //   mulh = 001
  //   mulhsu = 010
  //   mulhu = 011
  //   div = 100
  //   divu = 101
  //   Select control
  //   rem = 110
  //   remu = 111
endmodule

module MULTEST (
  input  [3:0] dataA,
  input  [3:0] dataB,
  input  [2:0] sel,
  output [3:0] OutData
);

  wire and_4_out, and_5_out, divSign, signedDiv;
  wire [3:0] and_1_out, and_2_out, and_6_out, and_7_out, data_a_pre_div, data_b_pre_div, div, divOut,
       divSignExt, mul, mul_h_out, mulh, mulhsu, rem_t, remOut, remSignExt, signAExt, signBExt, signDivExt,
       xor_1_out, xor_2_out, xor_3_out, xor_4_out, xor_6_out, xor_7_out;

  // Probe on dataA
  // Probe on dataA
  // Probe on dataB
  // Probe on dataB
  // Probe on OutData
  assign and_1_out = signDivExt & signAExt;  // AND_Gate and_1, 4 bits wide
  assign and_2_out = signDivExt & signBExt;  // AND_Gate and_2, 4 bits wide
  assign signAExt = {{3{dataA[3]}}, dataA[3]};  // Bit_Extender bit_extender_1
  assign signBExt = {{3{dataB[3]}}, dataB[3]};  // Bit_Extender bit_extender_2
  and and_3 (signedDiv, ~sel[0], sel[2]);  // AND_Gate
  assign signDivExt = {{3{signedDiv}}, signedDiv};  // Bit_Extender bit_extender_3
  assign xor_1_out = dataB ^ and_2_out;  // XOR_Gate xor_1, 4 bits wide
  assign xor_2_out = dataA ^ and_1_out;  // XOR_Gate xor_2, 4 bits wide
  and and_4 (and_4_out, dataB[3], signedDiv);
  and and_5 (and_5_out, dataA[3], signedDiv);
  Adder #(.width(4)) adder_1 (.a(xor_2_out), .b(4'b0000), .out(data_a_pre_div), .cin(and_5_out));  // open: cout
  // Probe on data_b_pre_div
  Adder #(.width(4)) adder_2 (.a(xor_1_out), .b(4'b0000), .out(data_b_pre_div), .cin(and_4_out));  // open: cout
  // Probe on data_a_pre_div
  // Probe on mul_h_out
  // Probe on mul
  Multiplier #(.width(4)) multiplier_1 (.a(dataA), .b(dataB), .out(mul), .cout(mul_h_out));  // open: cin
  Divider #(.width(4)) divider_1 (.a(data_a_pre_div), .b(data_b_pre_div), .out(divOut), .rem(remOut));  // open: upper
  assign xor_3_out = dataB ^ signAExt;  // XOR_Gate xor_3, 4 bits wide
  assign xor_4_out = dataA ^ signBExt;  // XOR_Gate xor_4, 4 bits wide
  xor xor_5 (divSign, dataA[3], dataB[3]);
  assign divSignExt = {{3{divSign}}, divSign};  // Bit_Extender bit_extender_4
  assign remSignExt = {{3{dataA[3]}}, dataA[3]};  // Bit_Extender bit_extender_5
  assign and_6_out = signAExt & xor_3_out;  // AND_Gate and_6, 4 bits wide
  assign and_7_out = signBExt & xor_4_out;  // AND_Gate and_7, 4 bits wide
  Adder #(.width(4)) adder_3 (.a(mul_h_out), .b(and_6_out), .out(mulhsu), .cin(dataA[3]));  // open: cout
  Adder #(.width(4)) adder_4 (.a(mulhsu), .b(and_7_out), .out(mulh), .cin(dataB[3]));  // open: cout
  // Probe on mulhsu
  // Probe on mulh
  assign xor_6_out = divOut ^ divSignExt;  // XOR_Gate xor_6, 4 bits wide
  Adder #(.width(4)) adder_5 (.a(xor_6_out), .b(4'b0000), .out(div), .cin(divSign));  // open: cout
  assign xor_7_out = remOut ^ remSignExt;  // XOR_Gate xor_7, 4 bits wide
  Adder #(.width(4)) adder_6 (.a(xor_7_out), .b(4'b0000), .out(rem_t), .cin(dataA[3]));  // open: cout
  // Probe on mul
  // Probe on mulh
  // Probe on mulhsu
  // Probe on mul_h_out
  // Probe on div
  // Probe on rem_t
  // Probe on divOut
  // Probe on remOut
  Multiplexer #(.select(3), .width(4)) multiplexer_1 (
    .in0(mul), .in1(mulh), .in2(mulhsu), .in3(mul_h_out), .in4(div), .in5(divOut), .in6(rem_t), .in7(remOut),
    .out(OutData), .sel(sel));
  // Probe on OutData

  // Other names for the same wires on the sheet: remSign = dataA[3]; signA = dataA[3]; signB = dataB[3];
  //   divSigned[3:0] = div; divu[3:0] = divOut; mul_out[3:0] = mul; mulhu[3:0] = mul_h_out; remSigned[3:0] = rem_t;
  //   remu[3:0] = remOut; sub_a_out[3:0] = mulh; sub_b_out[3:0] = mulhsu

  // Notes on the sheet:
  //   unsigned
  //   signed
  //   unsigned
  //   signed
  //   Multiply Signals
  //   Divide Signals
  //   Divide Pre-Process
  //   Multiply
  //   Divide
  //   Multiply Post Process
  //   Divide Post Process
  //   No corrections
  //   Apply both corrections
  //   Only apply B correction
  //   No corrections
  //   Multiply Output
  //   Divide Output
  //   mul = 000
  //   mulh = 001
  //   mulhsu = 010
  //   mulhu = 011
  //   div = 100
  //   divu = 101
  //   rem = 110
  //   remu = 111
  //   Select control
endmodule
