// Logisim project RiskVCPU.circ as structural Verilog: 6 circuits, main circuit RiskVCPU
module RiskVCPU (
  input  SysClk,
  input  Reset,
  input  PCWEn,
  input  [31:0] Instruction
);

  wire ASel, BSel, ebreak, ecall, EX_MEM_ebreak, EX_MEM_ecall, EX_MEM_MemRead, EX_MEM_MemWrite,
       EX_MEM_RegWEn, ID_EX_ASel, ID_EX_BSel, ID_EX_ebreak, ID_EX_ecall, ID_EX_FLUSH, ID_EX_MemRead,
       ID_EX_MemWrite, ID_EX_RegWEn, IF_ID_FLUSH, IF_ID_WE, MEM_WB_ebreak, MEM_WB_ecall, MEM_WB_RegWEn,
       MemRead, MemWrite, PC_WE, PCSel, RegWEn, SysClk_t;
  wire [1:0] AddrOffset, EX_MEM_WBSel, FWD_A, FWD_B, ID_EX_WBSel, MEM_WB_WBSel, WBSel;
  wire [2:0] EX_MEM_MemByteSel, ID_EX_MemByteSel, ImmSel, MemByteSel;
  wire [3:0] StoreMask;
  wire [4:0] ALUSel, BrSel, EX_MEM_rdi, ID_EX_ALUSel, ID_EX_BrSel, ID_EX_rdi, ID_EX_rs1, ID_EX_rs2,
       MEM_WB_rdi, rdi, rs1, rs2;
  wire [6:0] op_code;
  wire [31:0] ALUOut, EX_MEM_ALUOut, EX_MEM_PC, EX_MEM_PC_4, EX_MEM_RDataB, ID_EX_Imm, ID_EX_PC, ID_EX_PC_4,
       ID_EX_RDataA, ID_EX_RDataB, IF_ID_Inst, IF_ID_PC, IF_ID_PC_4, ImmGenOut, Inst, MEM_WB_ALUOut,
       MEM_WB_MemOut, MEM_WB_PC, MEM_WB_PC_4, MEM_WB_RegWBData, MemInAligned, MemOut, MemOutAligned,
       MemWriteData, PC, PCPlus4, RDataA, RDataB, RegWBData;

  Clock clock_1 (.out(SysClk_t));
  // Probe on ALUOut
  // Probe on PC
  // Probe on PCPlus4
  // Probe on Inst
  ProgramCounter programcounter_1 (
    .TargetAddr(ALUOut), .BranchCtl(PCSel), .PCWEn(PC_WE), .Clk(SysClk_t), .Reset(1'b0), .PcOut(PC),
    .PcPlus4(PCPlus4));
  IMem imem_1 (.PC(PC), .Inst(Inst));
  PipelineReg32Bit ID_ID_INST (.DataIn(Inst), .WE(IF_ID_WE), .FLUSH(IF_ID_FLUSH), .clk(SysClk_t), .DataOut(IF_ID_Inst));
  PipelineReg32Bit u_IF_ID_PC (.DataIn(PC), .WE(IF_ID_WE), .clk(SysClk_t), .DataOut(IF_ID_PC));  // open: FLUSH
  PipelineReg32Bit u_IF_ID_PC_4 (.DataIn(PCPlus4), .WE(IF_ID_WE), .clk(SysClk_t), .DataOut(IF_ID_PC_4));  // open: FLUSH
  // Probe on ImmGenOut
  // Probe on RDataA
  // Probe on RDataB
  // Probe on RegWBData
  MainController maincontroller_1 (
    .Inst(IF_ID_Inst), .ImmSel(ImmSel), .ASel(ASel), .BSel(BSel), .ALUSel(ALUSel), .BrSel(BrSel),
    .MemRead(MemRead), .MemWrite(MemWrite), .MemByteSel(MemByteSel), .RegWEn(RegWEn), .WBSel(WBSel),
    .Is_Ecall(ecall), .Is_Ebreak(ebreak), .rdi(rdi), .rs1(rs1), .rs2(rs2), .op_code(op_code));
  ImmGen immgen_1 (.InstIn(IF_ID_Inst), .ImmSelIn(ImmSel), .ImmOut(ImmGenOut));
  RegisterFile registerfile_1 (
    .Data(MEM_WB_RegWBData), .RdAddr(MEM_WB_rdi), .Rs1Addr(rs1), .Rs2Addr(rs2), .WriteEnable(MEM_WB_RegWEn),
    .Clk(SysClk_t), .DataA(RDataA), .DataB(RDataB));
  // Probe on ImmSel
  // Probe on ASel
  // Probe on BSel
  // Probe on ALUSel
  // Probe on BrSel
  // Probe on MemRead
  // Probe on MemWrite
  // Probe on MemByteSel
  // Probe on RegWEn
  // Probe on WBSel
  // Probe on ecall
  // Probe on ebreak
  // Probe on rdi
  // Probe on rs1
  // Probe on rs2
  PipelineReg32Bit u_ID_EX_RDataA (
    .DataIn(RDataA), .WE(1'b1), .FLUSH(ID_EX_FLUSH), .clk(SysClk_t), .DataOut(ID_EX_RDataA));
  PipelineReg32Bit u_ID_EX_RDataB (
    .DataIn(RDataB), .WE(1'b1), .FLUSH(ID_EX_FLUSH), .clk(SysClk_t), .DataOut(ID_EX_RDataB));
  PipelineReg32Bit u_ID_EX_Imm (
    .DataIn(ImmGenOut), .WE(1'b1), .FLUSH(ID_EX_FLUSH), .clk(SysClk_t), .DataOut(ID_EX_Imm));
  PipelineReg1Bit u_ID_EX_ASel (.DataIn(ASel), .WE(1'b1), .FLUSH(ID_EX_FLUSH), .clk(SysClk_t), .DataOut(ID_EX_ASel));
  PipelineReg1Bit u_ID_EX_BSel (.DataIn(BSel), .WE(1'b1), .FLUSH(ID_EX_FLUSH), .clk(SysClk_t), .DataOut(ID_EX_BSel));
  PipelineReg5Bit u_ID_EX_ALUSel (
    .DataIn(ALUSel), .WE(1'b1), .FLUSH(ID_EX_FLUSH), .clk(SysClk_t), .DataOut(ID_EX_ALUSel));
  PipelineReg5Bit u_ID_EX_BrSel (.DataIn(BrSel), .WE(1'b1), .FLUSH(ID_EX_FLUSH), .clk(SysClk_t), .DataOut(ID_EX_BrSel));
  PipelineReg1Bit u_ID_EX_MemRead (
    .DataIn(MemRead), .WE(1'b1), .FLUSH(ID_EX_FLUSH), .clk(SysClk_t), .DataOut(ID_EX_MemRead));
  PipelineReg1Bit u_ID_EX_MemWrite (
    .DataIn(MemWrite), .WE(1'b1), .FLUSH(ID_EX_FLUSH), .clk(SysClk_t), .DataOut(ID_EX_MemWrite));
  PipelineReg3Bit u_ID_EX_MemByteSel (
    .DataIn(MemByteSel), .WE(1'b1), .FLUSH(ID_EX_FLUSH), .clk(SysClk_t), .DataOut(ID_EX_MemByteSel));
  PipelineReg1Bit u_ID_EX_RegWEn (
    .DataIn(RegWEn), .WE(1'b1), .FLUSH(ID_EX_FLUSH), .clk(SysClk_t), .DataOut(ID_EX_RegWEn));
  PipelineReg2Bit u_ID_EX_WBSel (.DataIn(WBSel), .WE(1'b1), .FLUSH(ID_EX_FLUSH), .clk(SysClk_t), .DataOut(ID_EX_WBSel));
  PipelineReg1Bit u_ID_EX_ecall (.DataIn(ecall), .WE(1'b1), .FLUSH(ID_EX_FLUSH), .clk(SysClk_t), .DataOut(ID_EX_ecall));
  PipelineReg1Bit u_ID_EX_ebreak (
    .DataIn(ebreak), .WE(1'b1), .FLUSH(ID_EX_FLUSH), .clk(SysClk_t), .DataOut(ID_EX_ebreak));
  PipelineReg5Bit u_ID_EX_rdi (.DataIn(rdi), .WE(1'b1), .FLUSH(ID_EX_FLUSH), .clk(SysClk_t), .DataOut(ID_EX_rdi));
  PipelineReg5Bit u_ID_EX_rs1 (.DataIn(rs1), .WE(1'b1), .FLUSH(ID_EX_FLUSH), .clk(SysClk_t), .DataOut(ID_EX_rs1));
  PipelineReg5Bit u_ID_EX_rs2 (.DataIn(rs2), .WE(1'b1), .FLUSH(ID_EX_FLUSH), .clk(SysClk_t), .DataOut(ID_EX_rs2));
  PipelineReg32Bit u_ID_EX_PC (.DataIn(IF_ID_PC), .WE(1'b1), .clk(SysClk_t), .DataOut(ID_EX_PC));  // open: FLUSH
  PipelineReg32Bit u_ID_EX_PC_4 (.DataIn(IF_ID_PC_4), .WE(1'b1), .clk(SysClk_t), .DataOut(ID_EX_PC_4));  // open: FLUSH
  // Probe on PCSel
  // Probe on ALUOut
  HazardControl hazardcontrol_1 (
    .PCSel(PCSel), .IF_ID_rs1(rs1), .IF_ID_rs2(rs2), .ID_EX_rs1(ID_EX_rs1), .ID_EX_rs2(ID_EX_rs2),
    .ID_EX_rdi(ID_EX_rdi), .ID_EX_MemRead(ID_EX_MemRead), .ID_EX_RegWEn(ID_EX_RegWEn),
    .EX_MEM_rdi(EX_MEM_rdi), .EX_MEM_RegWEn(EX_MEM_RegWEn), .MEM_WB_rdi(MEM_WB_rdi),
    .MEM_WB_RegWEn(MEM_WB_RegWEn), .PC_WE(PC_WE), .IF_ID_WE(IF_ID_WE), .ID_ID_FLUSH(IF_ID_FLUSH),
    .ID_EX_FLUSH(ID_EX_FLUSH), .FWD_A(FWD_A), .FWD_B(FWD_B));
  BranchController branchcontroller_1 (
    .DataA(ID_EX_RDataA), .DataB(ID_EX_RDataB), .BrSel(ID_EX_BrSel), .TakeBranch(PCSel));
  ALUControl alucontrol_1 (
    .RDataA(ID_EX_RDataA), .PC(ID_EX_PC), .ASel(ID_EX_ASel), .RDataB(ID_EX_RDataB), .ImmVal(ID_EX_Imm),
    .BSel(ID_EX_BSel), .ALUSel(ID_EX_ALUSel), .FWD_A(FWD_A), .FWD_B(FWD_B), .DataOut(ALUOut));  // open: EX_MEM_ALUOut, MEM_WB_ALUOut
  PipelineReg32Bit u_EX_MEM_ALUOut (.DataIn(ALUOut), .WE(1'b1), .FLUSH(1'b0), .clk(SysClk_t), .DataOut(EX_MEM_ALUOut));
  PipelineReg32Bit u_EX_MEM_RDataB (
    .DataIn(ID_EX_RDataB), .WE(1'b1), .FLUSH(1'b0), .clk(SysClk_t), .DataOut(EX_MEM_RDataB));
  PipelineReg1Bit u_EX_MEM_MemRead (
    .DataIn(ID_EX_MemRead), .WE(1'b1), .FLUSH(1'b0), .clk(SysClk_t), .DataOut(EX_MEM_MemRead));
  PipelineReg1Bit u_EX_MEM_MemWrite (
    .DataIn(ID_EX_MemWrite), .WE(1'b1), .FLUSH(1'b0), .clk(SysClk_t), .DataOut(EX_MEM_MemWrite));
  PipelineReg3Bit u_EX_MEM_MemByteSel (
    .DataIn(ID_EX_MemByteSel), .WE(1'b1), .FLUSH(1'b0), .clk(SysClk_t), .DataOut(EX_MEM_MemByteSel));
  PipelineReg1Bit u_EX_MEM_RegWEn (
    .DataIn(ID_EX_RegWEn), .WE(1'b1), .FLUSH(1'b0), .clk(SysClk_t), .DataOut(EX_MEM_RegWEn));
  PipelineReg2Bit u_EX_MEM_WBSel (
    .DataIn(ID_EX_WBSel), .WE(1'b1), .FLUSH(1'b0), .clk(SysClk_t), .DataOut(EX_MEM_WBSel));
  PipelineReg1Bit u_EX_MEM_ecall (
    .DataIn(ID_EX_ecall), .WE(1'b1), .FLUSH(1'b0), .clk(SysClk_t), .DataOut(EX_MEM_ecall));
  PipelineReg1Bit u_EX_MEM_ebreak (
    .DataIn(ID_EX_ebreak), .WE(1'b1), .FLUSH(1'b0), .clk(SysClk_t), .DataOut(EX_MEM_ebreak));
  PipelineReg5Bit u_EX_MEM_rdi (.DataIn(ID_EX_rdi), .WE(1'b1), .FLUSH(1'b0), .clk(SysClk_t), .DataOut(EX_MEM_rdi));
  PipelineReg32Bit u_EX_MEM_PC (.DataIn(ID_EX_PC), .WE(1'b1), .clk(SysClk_t), .DataOut(EX_MEM_PC));  // open: FLUSH
  PipelineReg32Bit u_EX_MEM_PC_4 (
    .DataIn(ID_EX_PC_4), .WE(1'b1), .clk(SysClk_t), .DataOut(EX_MEM_PC_4));  // open: FLUSH
  // Probe on MemWriteData
  // Probe on EX_MEM_RDataB
  // Probe on AddrOffset
  // Probe on MemOut
  // Probe on MemInAligned
  // Probe on MemOutAligned
  // Probe on AddrOffset
  DMem dmem_1 (
    .MemAddr(EX_MEM_ALUOut), .MemWrite(EX_MEM_MemWrite), .MemRead(EX_MEM_MemRead), .StoreMast(StoreMask),
    .clk(SysClk_t), .WriteData(MemWriteData), .AddrOffset(AddrOffset), .MemOut(MemOut));
  StoreAligner storealigner_1 (
    .Data(EX_MEM_RDataB), .AddrOffset(AddrOffset), .ByteSel(EX_MEM_MemByteSel), .DataOut(MemWriteData),
    .MaskOut(StoreMask));
  LoadAligner loadaligner_1 (.AddrOffset(AddrOffset), .Data(MemOut), .ByteSel(EX_MEM_MemByteSel), .Out0(MemOutAligned));
  PipelineReg32Bit u_MEM_WB_MemOut (
    .DataIn(MemOutAligned), .WE(1'b1), .FLUSH(1'b0), .clk(SysClk_t), .DataOut(MEM_WB_MemOut));
  PipelineReg32Bit u_MEM_WB_ALUOut (
    .DataIn(EX_MEM_ALUOut), .WE(1'b1), .FLUSH(1'b0), .clk(SysClk_t), .DataOut(MEM_WB_ALUOut));
  PipelineReg1Bit u_MEM_WB_RegWEn (
    .DataIn(EX_MEM_RegWEn), .WE(1'b1), .FLUSH(1'b0), .clk(SysClk_t), .DataOut(MEM_WB_RegWEn));
  PipelineReg2Bit u_MEM_WB_WBSel (
    .DataIn(EX_MEM_WBSel), .WE(1'b1), .FLUSH(1'b0), .clk(SysClk_t), .DataOut(MEM_WB_WBSel));
  PipelineReg1Bit u_MEM_WB_ecall (
    .DataIn(EX_MEM_ecall), .WE(1'b1), .FLUSH(1'b0), .clk(SysClk_t), .DataOut(MEM_WB_ecall));
  PipelineReg1Bit u_MEM_WB_ebreak (
    .DataIn(EX_MEM_ebreak), .WE(1'b1), .FLUSH(1'b0), .clk(SysClk_t), .DataOut(MEM_WB_ebreak));
  PipelineReg5Bit u_MEM_WB_rdi (.DataIn(EX_MEM_rdi), .WE(1'b1), .FLUSH(1'b0), .clk(SysClk_t), .DataOut(MEM_WB_rdi));
  PipelineReg32Bit u_MEM_WB_PC (.DataIn(EX_MEM_PC), .WE(1'b1), .clk(SysClk_t), .DataOut(MEM_WB_PC));  // open: FLUSH
  PipelineReg32Bit u_MEM_WB_PC_4 (
    .DataIn(EX_MEM_PC_4), .WE(1'b1), .clk(SysClk_t), .DataOut(MEM_WB_PC_4));  // open: FLUSH
  // Probe on MEM_WB_WBSel
  // Probe on MEM_WB_RegWBData
  // WriteBackControl writebackcontrol_1: pin names not known; wires that end beside it: MEM_WB_ALUOut, MEM_WB_MemOut, MEM_WB_PC_4, MEM_WB_WBSel, MEM_WB_RegWBData

  // Notes on the sheet:
  //   IF - Instruction Fetch
  //   IF_ID
  //   ID - Instruction Decode
  //   ID_EX
  //   EX - Execute
  //   EX_MEM
  //   MEM - Memory
  //   MEM_WB
  //   00 = ALU
  //   01 = Mem
  //   11 = PCPlus4
  //   WB - Write Back
endmodule

module PipelineReg32Bit (
  input  [31:0] DataIn,
  input  WE,
  input  FLUSH,
  input  clk,
  output [31:0] DataOut
);

  wire or_1_out;
  wire [31:0] multiplexer_1_out;

  // Probe on multiplexer_1_out
  Multiplexer #(.width(32)) multiplexer_1 (.in0(DataIn), .in1({32{1'b0}}), .out(multiplexer_1_out), .sel(FLUSH));
  or or_1 (or_1_out, WE, FLUSH);
  Register #(.width(32)) register_1 (.D(multiplexer_1_out), .en(or_1_out), .clk(clk), .Q(DataOut));  // open: clr
  // Probe on DataOut

  // Other names for the same wires on the sheet: data[31:0] = DataIn
endmodule

module PipelineReg5Bit (
  input  [4:0] DataIn,
  input  WE,
  input  FLUSH,
  input  clk,
  output [4:0] DataOut
);

  wire or_1_out;
  wire [4:0] multiplexer_1_out;

  // Probe on multiplexer_1_out
  Multiplexer #(.width(5)) multiplexer_1 (.in0(DataIn), .in1({5{1'b0}}), .out(multiplexer_1_out), .sel(FLUSH));
  or or_1 (or_1_out, WE, FLUSH);
  Register #(.width(5)) register_1 (.D(multiplexer_1_out), .en(or_1_out), .clk(clk), .Q(DataOut));  // open: clr
  // Probe on DataOut

  // Other names for the same wires on the sheet: data[4:0] = DataIn
endmodule

module PipelineReg1Bit (
  input  DataIn,
  input  WE,
  input  FLUSH,
  input  clk,
  output DataOut
);

  wire multiplexer_1_out, or_1_out;

  // Probe on multiplexer_1_out
  Multiplexer multiplexer_1 (.in0(DataIn), .in1(1'b0), .out(multiplexer_1_out), .sel(FLUSH));
  or or_1 (or_1_out, WE, FLUSH);
  Register #(.width(1)) register_1 (.D(multiplexer_1_out), .en(or_1_out), .clk(clk), .Q(DataOut));  // open: clr
  // Probe on DataOut

  // Other names for the same wires on the sheet: data = DataIn
endmodule

module PipelineReg3Bit (
  input  [2:0] DataIn,
  input  WE,
  input  FLUSH,
  input  clk,
  output [2:0] DataOut
);

  wire or_1_out;
  wire [2:0] multiplexer_1_out;

  // Probe on multiplexer_1_out
  Multiplexer #(.width(3)) multiplexer_1 (.in0(DataIn), .in1(3'b000), .out(multiplexer_1_out), .sel(FLUSH));
  or or_1 (or_1_out, WE, FLUSH);
  Register #(.width(3)) register_1 (.D(multiplexer_1_out), .en(or_1_out), .clk(clk), .Q(DataOut));  // open: clr
  // Probe on DataOut

  // Other names for the same wires on the sheet: data[2:0] = DataIn
endmodule

module PipelineReg2Bit (
  input  [1:0] DataIn,
  input  WE,
  input  FLUSH,
  input  clk,
  output [1:0] DataOut
);

  wire or_1_out;
  wire [1:0] multiplexer_1_out;

  // Probe on multiplexer_1_out
  Multiplexer #(.width(2)) multiplexer_1 (.in0(DataIn), .in1(2'b00), .out(multiplexer_1_out), .sel(FLUSH));
  or or_1 (or_1_out, WE, FLUSH);
  Register #(.width(2)) register_1 (.D(multiplexer_1_out), .en(or_1_out), .clk(clk), .Q(DataOut));  // open: clr
  // Probe on DataOut

  // Other names for the same wires on the sheet: data[1:0] = DataIn
endmodule
