// Logisim project RiskVControl.circ as structural Verilog: 10 circuits, main circuit MainController
module MainController (
  input  [31:0] Inst,
  output [2:0] ImmSel,
  output ASel,
  output BSel,
  output [4:0] ALUSel,
  output [4:0] BrSel,
  output MemRead,
  output MemWrite,
  output [2:0] MemByteSel,
  output RegWEn,
  output [1:0] WBSel,
  output [11:0] CSRAddr,
  output [3:0] CSRCtl,
  output Is_Ecall,
  output Is_Ebreak,
  output [4:0] rdi,
  output [4:0] rs1,
  output [4:0] rs2,
  output [6:0] op_code
);

  wire and_1_out, and_2_out, and_3_out, and_4_out, and_5_out, and_6_out, and_7_out, AUIPC, BRANCH, JALR,
       LOAD, LUI, MISC_MEM, NOP, NOP_SYSTEM, not_1_out, OP, OP_32, OP_IMM, or_1_out, or_3_out, or_5_out,
       or_7_out, or_8_out, or_9_out, or_11_out, or_12_out, STORE, SYSTEM, zeroSrcRegs;
  wire [1:0] and_9_out, bit_extender_3_out;
  wire [2:0] bit_extender_1_out;
  wire [4:0] bit_extender_2_out;

  // Probe on Inst
  and and_1 (and_1_out, ~Inst[15], ~Inst[16], ~Inst[17], ~Inst[18], ~Inst[19]);  // AND_Gate
  and and_2 (and_2_out, ~Inst[20], ~Inst[21], ~Inst[22], ~Inst[23], ~Inst[24]);  // AND_Gate
  and and_3 (and_3_out, ~Inst[7], ~Inst[8], ~Inst[9], ~Inst[10], ~Inst[11]);  // AND_Gate
  and and_4 (and_4_out, ~Inst[25], ~Inst[26], ~Inst[27], ~Inst[28], ~Inst[29], ~Inst[30], ~Inst[31]);  // AND_Gate
  and and_5 (and_5_out, and_1_out, and_2_out, and_3_out, and_4_out);
  or or_1 (or_1_out, OP, OP_IMM);
  and and_6 (and_6_out, ~Inst[0], ~Inst[1], ~Inst[2], ~Inst[3], ~Inst[4], ~Inst[5], ~Inst[6]);  // AND_Gate
  or or_2 (NOP_SYSTEM, NOP, SYSTEM);
  // Probe on Inst[6:0]
  // Probe on Inst[14:12]
  // Probe on Inst[31:25]
  // Probe on Inst[11:7]
  // Probe on Inst[19:15]
  // Probe on Inst[24:20]
  or or_3 (or_3_out, or_1_out, and_6_out);
  and and_7 (and_7_out, or_3_out, and_5_out);
  or or_4 (NOP, MISC_MEM, and_7_out);
  Decoder #(.select(5)) decoder_1 (
    .out0(LOAD), .out3(MISC_MEM), .out4(OP_IMM), .out5(AUIPC), .out8(STORE), .out12(OP), .out13(LUI),
    .out14(OP_32), .out24(BRANCH), .out25(JALR), .out27(ImmSel[2]), .out28(SYSTEM), .sel(Inst[6:2]));  // open: out1, out2, out6, out7, out9, out10, out11, out15, out16, out17, out18, out19, out20, out21, out22, out23, out26, out29, out30, out31, en
  or or_5 (or_5_out, Inst[12], Inst[13], Inst[14]);
  or or_6 (zeroSrcRegs, ImmSel[2], LUI, AUIPC);
  and and_8 (CSRCtl[3], or_5_out, SYSTEM);
  not not_1 (not_1_out, OP_IMM);
  or or_7 (or_7_out, ImmSel[2], JALR);
  assign bit_extender_1_out = {{2{or_8_out}}, or_8_out};  // Bit_Extender bit_extender_1
  or or_8 (or_8_out, LOAD, STORE);
  or or_9 (or_9_out, LUI, AUIPC);
  or or_10 (ImmSel[1], or_9_out, BRANCH);
  assign bit_extender_2_out = {{4{or_11_out}}, or_11_out};  // Bit_Extender bit_extender_2
  or or_11 (or_11_out, OP_IMM, OP);
  assign and_9_out = {Inst[25], Inst[30]} & bit_extender_3_out;  // AND_Gate and_9, 2 bits wide
  assign bit_extender_3_out = {{1{not_1_out}}, not_1_out};  // Bit_Extender bit_extender_3
  and and_10 (BrSel[3], BRANCH, ~NOP);  // AND_Gate
  and and_11 (BrSel[4], or_7_out, ~NOP);  // AND_Gate
  and and_12 (MemRead, LOAD, ~NOP_SYSTEM);  // AND_Gate
  and and_13 (MemWrite, STORE, ~NOP_SYSTEM);  // AND_Gate
  assign MemByteSel = bit_extender_1_out & {Inst[13:12], Inst[14]};  // AND_Gate and_14, 3 bits wide
  or or_12 (or_12_out, OP, OP_IMM, LOAD, LUI, AUIPC, ImmSel[2], JALR, CSRCtl[3]);
  or or_13 (WBSel[0], LOAD, CSRCtl[3]);
  or or_14 (WBSel[1], ImmSel[2], JALR, CSRCtl[3]);
  and and_15 (Is_Ecall, SYSTEM, ~Inst[20]);  // AND_Gate
  and and_16 (Is_Ebreak, Inst[20], SYSTEM);
  Multiplexer #(.width(5)) multiplexer_1 (.in0(Inst[19:15]), .in1({5{1'b0}}), .out(rs1), .sel(zeroSrcRegs));
  Multiplexer #(.width(5)) multiplexer_2 (.in0(Inst[24:20]), .in1({5{1'b0}}), .out(rs2), .sel(zeroSrcRegs));
  or or_15 (ImmSel[0], or_9_out, STORE);
  assign ALUSel = bit_extender_2_out & {and_9_out, Inst[14:12]};  // AND_Gate and_17, 5 bits wide
  and and_18 (RegWEn, or_12_out, ~NOP);  // AND_Gate
  or or_16 (ASel, AUIPC, ImmSel[2], BRANCH);
  or or_17 (BSel, LUI, STORE, LOAD, OP_IMM, AUIPC, ImmSel[2], JALR, BRANCH);

  assign BrSel[2:0] = Inst[14:12];
  assign CSRAddr = Inst[31:20];
  assign CSRCtl[2:0] = Inst[14:12];
  assign op_code = Inst[6:0];
  assign rdi = Inst[11:7];

  // Other names for the same wires on the sheet: func7[6:0] = Inst[31:25]; func3[2:0] = Inst[14:12];
  //   CSRActive = CSRCtl[3]; JAL = ImmSel[2]; rs1_t[4:0] = Inst[19:15]; rs2_t[4:0] = Inst[24:20]

  // Notes on the sheet:
  //   NOP = All regsiters are ZERO and func7 is ZERO
  //   OPCODE DECODE
  //   OP_IMM == 00100 == 4
  //   STORE == 01000 == 8
  //   OP == 01100 == 12
  //   LUI == 01101 == 13
  //   BRANCH == 11000 == 24
  //   JAL == 11011 == 27
  //   LOAD == 00000 == 0
  //   MISC_MEM == 00011 == 3
  //   AUIPC == 00101 == 5
  //   SYSTEM == 11100 == 28
  //   OP_32 == 01110 == 14
  //   JALR == 11001 == 25
  //   Register Index
  //   ID_Control
  //   EX_Control
  //   MEM_Control
  //   WB_Control
  //   CSR Control
  //   Trap_Control
  //   Bus to control which bytes are active during memory read and write
  //   MemByteSel[0] = func3[2]
  //   MemByteSel[1] = func3[0]
  //   MemByteSel[2] = func3[1]
  //   Sent directly to ALUController
  //   (1 bit): Breakpoint trap flag.
  //   (3bit):  Send to ImmGen Sel input
  //   ImmSel[0] = Store OR LUI OR AUIPC
  //   ImmSel[1] = Branch OR LUI OR AUIPC
  //   ImmSel[2] = JAL
  //   (1 bit): Selects ALU operand A
  //   ASel = AUIPC OR Branch OR JAL
  //   ALUSel[0] = funct3[0]
  //   ALUSel[1] = funct3[1]
  //   ALUSel[2] = funct3[2]
  //   (1 bit): Enables Data Memory read operations.
  //   (1 bit): Enables Data Memory write operations.
  //   (1 bit): Master write-enable for the register file.
  //   (2 bit): Selects the writeback source (ALU result vs. Memory read data).
  //   (1 bit): Selects the writeback source (ALU result vs. Memory read data).
  //   (1 bit): Selects ALU operand B (Register vs. Immediate).
  //   BSel = IType OR Load OR Store OR AUIPC OR JAL OR JALR
  //   ALUSel[3] = funct7[5] AND (RType OR IShift_Right)
  //   ALUSel[4] = funct7[0] AND (RType OR IShift_Right)
  //   (4bit): 3 Bit branch selector code sent directly to the BranchControl
endmodule

module BranchController (
  input  [31:0] DataA,
  input  [31:0] DataB,
  input  [4:0] BrSel,
  output TakeBranch
);

  wire adder_1_cout, and_1_out, branchselector_1_takebranch, EQ, LTS, LTU;
  wire [31:0] adder_1_out, not_1_out;

  assign not_1_out = ~DataB;  // NOT_Gate not_1, 32 bits wide
  Adder #(.width(32)) adder_1 (.a(DataA), .b(not_1_out), .out(adder_1_out), .cin(1'b1), .cout(adder_1_cout));
  BranchSelector branchselector_1 (
    .EQ(EQ), .LTS(LTS), .LTU(LTU), .sel(BrSel[2:0]), .TakeBranch(branchselector_1_takebranch));
  and and_1 (and_1_out, branchselector_1_takebranch, BrSel[3]);
  BranchComparator branchcomparator_1 (
    .InSum(adder_1_out), .InCout(adder_1_cout), .ASignIn(DataA[31]), .BSignIn(DataB[31]), .EQ(EQ), .LTU(LTU),
    .LTS(LTS));
  or or_1 (TakeBranch, and_1_out, BrSel[4]);

  // Other names for the same wires on the sheet: ASign = DataA[31]; BSign = DataB[31]
endmodule

module BranchComparator (
  input  [31:0] InSum,
  input  InCout,
  input  ASignIn,
  input  BSignIn,
  output EQ,
  output LTU,
  output LTS
);

  wire or_1_out, xor_1_out;

  not not_1 (LTU, InCout);
  xor xor_1 (xor_1_out, ASignIn, BSignIn);
  Multiplexer multiplexer_1 (.in0(LTU), .in1(ASignIn), .out(LTS), .sel(xor_1_out));
  or or_1 (or_1_out, InSum[0], InSum[1], InSum[2], InSum[3], InSum[4], InSum[5], InSum[6], InSum[7], InSum[8], InSum[9], InSum[10], InSum[11], InSum[12], InSum[13], InSum[14], InSum[15], InSum[16], InSum[17], InSum[18], InSum[19], InSum[20], InSum[21], InSum[22], InSum[23], InSum[24], InSum[25], InSum[26], InSum[27], InSum[28], InSum[29], InSum[30], InSum[31]);
  not not_2 (EQ, or_1_out);
endmodule

module BranchSelector (
  input  EQ,
  input  LTS,
  input  LTU,
  input  [2:0] sel,
  output TakeBranch
);

  wire not_1_out, or_1_out, or_2_out;

  not not_1 (not_1_out, EQ);
  or or_1 (or_1_out, ~LTS, EQ);  // OR_Gate
  or or_2 (or_2_out, ~LTU, EQ);  // OR_Gate
  Multiplexer #(.select(3)) multiplexer_1 (
    .in0(EQ), .in1(not_1_out), .in2(1'b0), .in3(1'b0), .in4(LTS), .in5(or_1_out), .in6(LTU), .in7(or_2_out),
    .out(TakeBranch), .sel(sel));
endmodule

module ImmGen (
  input  [31:0] InstIn,
  input  [2:0] ImmSelIn,
  output [31:0] ImmOut
);

  Multiplexer #(.select(3), .width(32)) multiplexer_1 (
    .in0({{21{InstIn[31]}}, InstIn[30:20]}), .in1({{21{InstIn[31]}}, InstIn[30:25], InstIn[11:7]}),
    .in2({{20{InstIn[31]}}, InstIn[7], InstIn[30:25], InstIn[11:8], 1'b0}),
    .in3({InstIn[31:12], {12{1'b0}}}),
    .in4({{12{InstIn[31]}}, InstIn[19:12], InstIn[20], InstIn[30:21], 1'b0}), .out(ImmOut), .sel(ImmSelIn));  // open: in5, in6, in7

  // Other names for the same wires on the sheet: BType[31:1] = {{20{InstIn[31]}}, InstIn[7], InstIn[30:25], InstIn[11:8]};
  //   Ins8 = InstIn[8]; SType[31:0] = {{21{InstIn[31]}}, InstIn[30:25], InstIn[11:7]}; Ins9 = InstIn[9];
  //   Ins10 = InstIn[10]; Ins11 = InstIn[11]; Ins7 = InstIn[7]; ImmSel[2:0] = ImmSelIn; Ins0 = InstIn[0];
  //   Ins1 = InstIn[1]; Ins2 = InstIn[2]; Ins3 = InstIn[3]; Ins4 = InstIn[4]; Ins5 = InstIn[5]; Ins6 = InstIn[6];
  //   Ins21 = InstIn[21]; IType[31:0] = {{21{InstIn[31]}}, InstIn[30:20]};
  //   JType[31:1] = {{12{InstIn[31]}}, InstIn[19:12], InstIn[20], InstIn[30:21]}; UType[31:12] = InstIn[31:12];
  //   Ins22 = InstIn[22]; Ins23 = InstIn[23]; Ins24 = InstIn[24]; Ins25 = InstIn[25]; Ins26 = InstIn[26];
  //   Ins27 = InstIn[27]; Ins28 = InstIn[28]; Ins29 = InstIn[29]; Ins30 = InstIn[30]; Ins20 = InstIn[20];
  //   Ins12 = InstIn[12]; Ins13 = InstIn[13]; Ins14 = InstIn[14]; Ins15 = InstIn[15]; Ins16 = InstIn[16];
  //   Ins17 = InstIn[17]; Ins18 = InstIn[18]; Ins19 = InstIn[19]; Ins31 = InstIn[31]

  // Notes on the sheet:
  //   I-Type
  //   S-Type
  //   B-Type
  //   U-Type
  //   J-Type
endmodule

module ProgramCounter (
  input  [31:0] TargetAddr,
  input  BranchCtl,
  input  PCWEn,
  input  Clk,
  input  Reset,
  output [31:0] PcOut,
  output [31:0] PcPlus4
);

  wire [31:0] multiplexer_1_out;

  Multiplexer #(.width(32)) multiplexer_1 (.in0(PcPlus4), .in1(TargetAddr), .out(multiplexer_1_out), .sel(BranchCtl));
  Register #(.width(32)) register_1 (.D(multiplexer_1_out), .en(PCWEn), .clk(Clk), .Q(PcOut), .clr(Reset));
  Adder #(.width(32)) adder_1 (.a(32'h4), .b(PcOut), .out(PcPlus4));  // open: cin, cout
endmodule

module WriteBackControl (
  input  [31:0] ALUOut,
  input  [31:0] MemOut,
  input  [31:0] PCPlus4,
  input  [31:0] CSROut,
  input  [1:0] WBSel,
  output [31:0] OutData
);

  // Probe on OutData
  Multiplexer #(.select(2), .width(32)) multiplexer_1 (
    .in0(ALUOut), .in1(MemOut), .in2(PCPlus4), .in3(CSROut), .out(OutData), .sel(WBSel));
  // Probe on WBSel

  // Other names for the same wires on the sheet: CSR[31:0] = CSROut; MemOutAligned[31:0] = MemOut;
  //   RegWBData[31:0] = OutData

  // Notes on the sheet:
  //   00 = ALU
  //   01 = Mem
  //   10 = PCPlus4
  //   11 = CSR
endmodule

module HazardControl (
  input  PCSel,
  input  [4:0] IF_ID_rs1,
  input  [4:0] IF_ID_rs2,
  input  [4:0] ID_EX_rs1,
  input  [4:0] ID_EX_rs2,
  input  [4:0] ID_EX_rdi,
  input  ID_EX_MemRead,
  input  ID_EX_RegWEn,
  input  [3:0] ID_EX_CSRCtl,
  input  [4:0] EX_MEM_rdi,
  input  EX_MEM_RegWEn,
  input  [3:0] EX_MEM_CSRCtl,
  input  [4:0] MEM_WB_rdi,
  input  MEM_WB_RegWEn,
  output PC_WE,
  output IF_ID_WE,
  output IF_ID_FLUSH,
  output ID_EX_FLUSH,
  output [1:0] FWD_A,
  output [1:0] FWD_B
);

  wire and_1_out, CSR_stall, EX_MEM_rdi_NOT_ZERO, ID_EX_rdi_NOT_ZERO, Load_Use_Stall, MEM_WB_ALUOutSel_A,
       MEM_WB_ALUOutSel_B, MEM_WB_rdi_NOT_ZERO, or_4_out, rs1_EQ_EX_MEM_rdi, rs1_EQ_MEM_WB_rdi,
       rs2_EQ_EX_MEM_rdi, rs2_EQ_MEM_WB_rdi, xorcomparitor_5_eq, xorcomparitor_6_eq;

  XORComparitor xorcomparitor_1 (.A(ID_EX_rs1), .B(EX_MEM_rdi), .EQ(rs1_EQ_EX_MEM_rdi));
  XORComparitor xorcomparitor_2 (.A(ID_EX_rs1), .B(MEM_WB_rdi), .EQ(rs1_EQ_MEM_WB_rdi));
  XORComparitor xorcomparitor_3 (.A(ID_EX_rs2), .B(EX_MEM_rdi), .EQ(rs2_EQ_EX_MEM_rdi));
  XORComparitor xorcomparitor_4 (.A(ID_EX_rs2), .B(MEM_WB_rdi), .EQ(rs2_EQ_MEM_WB_rdi));
  XORComparitor xorcomparitor_5 (.A(ID_EX_rdi), .B(IF_ID_rs1), .EQ(xorcomparitor_5_eq));
  XORComparitor xorcomparitor_6 (.A(IF_ID_rs2), .B(ID_EX_rdi), .EQ(xorcomparitor_6_eq));
  or or_1 (ID_EX_rdi_NOT_ZERO, ~ID_EX_rdi[0], ~ID_EX_rdi[1], ~ID_EX_rdi[2], ~ID_EX_rdi[3], ~ID_EX_rdi[4]);  // OR_Gate
  or or_2 (EX_MEM_rdi_NOT_ZERO, ~EX_MEM_rdi[0], ~EX_MEM_rdi[1], ~EX_MEM_rdi[2], ~EX_MEM_rdi[3], ~EX_MEM_rdi[4]);  // OR_Gate
  or or_3 (MEM_WB_rdi_NOT_ZERO, ~MEM_WB_rdi[0], ~MEM_WB_rdi[1], ~MEM_WB_rdi[2], ~MEM_WB_rdi[3], ~MEM_WB_rdi[4]);  // OR_Gate
  and and_1 (and_1_out, ID_EX_MemRead, ID_EX_rdi_NOT_ZERO);
  or or_4 (or_4_out, xorcomparitor_5_eq, xorcomparitor_6_eq);
  and and_2 (Load_Use_Stall, and_1_out, or_4_out);
  and and_3 (FWD_A[0], EX_MEM_rdi_NOT_ZERO, rs1_EQ_EX_MEM_rdi, EX_MEM_RegWEn);
  and and_4 (MEM_WB_ALUOutSel_A, MEM_WB_rdi_NOT_ZERO, rs1_EQ_MEM_WB_rdi, MEM_WB_RegWEn);
  and and_5 (FWD_B[0], EX_MEM_rdi_NOT_ZERO, rs2_EQ_EX_MEM_rdi, EX_MEM_RegWEn);
  and and_6 (MEM_WB_ALUOutSel_B, MEM_WB_rdi_NOT_ZERO, rs2_EQ_MEM_WB_rdi, MEM_WB_RegWEn);
  or or_5 (CSR_stall, ID_EX_CSRCtl[3], EX_MEM_CSRCtl[3]);
  and and_7 (PC_WE, ~Load_Use_Stall, ~CSR_stall);  // AND_Gate
  and and_8 (IF_ID_WE, ~Load_Use_Stall, ~CSR_stall);  // AND_Gate
  or or_6 (ID_EX_FLUSH, Load_Use_Stall, PCSel, CSR_stall);
  and and_9 (FWD_A[1], ~FWD_A[0], MEM_WB_ALUOutSel_A);  // AND_Gate
  and and_10 (FWD_B[1], ~FWD_B[0], MEM_WB_ALUOutSel_B);  // AND_Gate

  assign IF_ID_FLUSH = PCSel;

  // Other names for the same wires on the sheet: EX_MEM_active_csr = EX_MEM_CSRCtl[3]; EX_MEM_ALUOutSel_A = FWD_A[0];
  //   EX_MEM_ALUOutSel_B = FWD_B[0]; ID_EX_active_csr = ID_EX_CSRCtl[3]

  // Notes on the sheet:
  //   IF_ID
  //   ID_EX
  //   EX_MEM
  //   MEM_WB
  //   FWD_A Data Hazard
  //   EX_MEM_rdi == ID_EX_rs1 (1 cycle ahead)
  //   MEM_WB_rdi == ID_EX_rs1 (2 cycles ahead)
  //   FWD_B Data Hazard
  //   EX_MEM_rdi == ID_EX_rs2 (1 cycle ahead)
  //   MEM_WB_rdi == ID_EX_rs2 (2 cycles ahead)
  //   Load_Use_Stall = ID_EX_MemRead AND (ID_EX_rdi != 0) AND ((ID_EX_rdi == IF_ID_rs1) OR (ID_EX_rdi == IF_ID_rs2));
  //   CSR Stall
  //   Forward Control
  //   IF_ID
  //   ID_EX
endmodule

module ForwardControl (
  input  [31:0] ID_EX_RDataA,
  input  [31:0] ID_EX_RDataB,
  input  [31:0] EX_MEM_ALUOut,
  input  [31:0] WB_RegData,
  input  [1:0] FWD_A,
  input  [1:0] FWD_B,
  output [31:0] RDataA,
  output [31:0] RDataB
);

  Multiplexer #(.select(2), .width(32)) multiplexer_1 (
    .in0(ID_EX_RDataA), .in1(EX_MEM_ALUOut), .in2(WB_RegData), .out(RDataA), .sel(FWD_A));  // open: in3
  Multiplexer #(.select(2), .width(32)) multiplexer_2 (
    .in0(ID_EX_RDataB), .in1(EX_MEM_ALUOut), .in2(WB_RegData), .out(RDataB), .sel(FWD_B));  // open: in3
endmodule

module XORComparitor (
  input  [4:0] A,
  input  [4:0] B,
  output EQ
);

  wire [4:0] xor_1_out;

  assign xor_1_out = A ^ B;  // XOR_Gate xor_1, 5 bits wide
  and and_1 (EQ, ~xor_1_out[0], ~xor_1_out[1], ~xor_1_out[2], ~xor_1_out[3], ~xor_1_out[4]);  // AND_Gate
endmodule
