// Logisim project RiskVMemory.circ as structural Verilog: 9 circuits, main circuit RegisterFile
module RegisterFile (
  input  [31:0] Data,
  input  [4:0] RdAddr,
  input  [4:0] Rs1Addr,
  input  [4:0] Rs2Addr,
  input  WriteEnable,
  input  Clk,
  output [31:0] DataA,
  output [31:0] DataB,
  output [31:0] TEST_x31Data
);

  wire and_1_out, and_2_out, rd_not_zero, rs1_EQ_rdi, rs2_EQ_rdi, x1_we, x2_we, x3_we, x4_we, x5_we, x6_we,
       x7_we, x8_we, x9_we, x10_we, x11_we, x12_we, x13_we, x14_we, x15_we, x16_we, x17_we, x18_we, x19_we,
       x20_we, x21_we, x22_we, x23_we, x24_we, x25_we, x26_we, x27_we, x28_we, x29_we, x30_we, x31_we;
  wire [31:0] DataA_t, DataB_t, x1, x2, x3, x4, x5, x6, x7, x8, x9, x10, x11, x12, x13, x14, x15, x16, x17,
       x18, x19, x20, x21, x22, x23, x24, x25, x26, x27, x28, x29, x30;

  Demultiplexer #(.select(5)) demultiplexer_1 (
    .out1(x1_we), .out2(x2_we), .out3(x3_we), .out4(x4_we), .out5(x5_we), .out6(x6_we), .out7(x7_we),
    .out8(x8_we), .out9(x9_we), .out10(x10_we), .out11(x11_we), .out12(x12_we), .out13(x13_we),
    .out14(x14_we), .out15(x15_we), .out16(x16_we), .out17(x17_we), .out18(x18_we), .out19(x19_we),
    .out20(x20_we), .out21(x21_we), .out22(x22_we), .out23(x23_we), .out24(x24_we), .out25(x25_we),
    .out26(x26_we), .out27(x27_we), .out28(x28_we), .out29(x29_we), .out30(x30_we), .out31(x31_we),
    .in(WriteEnable), .sel(RdAddr));  // open: out0
  Register #(.width(32)) register_1 (.D(Data), .en(x1_we), .clk(Clk), .Q(x1));  // open: clr
  Register #(.width(32)) register_2 (.D(Data), .en(x2_we), .clk(Clk), .Q(x2));  // open: clr
  Register #(.width(32)) register_3 (.D(Data), .en(x3_we), .clk(Clk), .Q(x3));  // open: clr
  Register #(.width(32)) register_4 (.D(Data), .en(x4_we), .clk(Clk), .Q(x4));  // open: clr
  Register #(.width(32)) register_5 (.D(Data), .en(x5_we), .clk(Clk), .Q(x5));  // open: clr
  Register #(.width(32)) register_6 (.D(Data), .en(x6_we), .clk(Clk), .Q(x6));  // open: clr
  Register #(.width(32)) register_7 (.D(Data), .en(x7_we), .clk(Clk), .Q(x7));  // open: clr
  Register #(.width(32)) register_8 (.D(Data), .en(x8_we), .clk(Clk), .Q(x8));  // open: clr
  Register #(.width(32)) register_9 (.D(Data), .en(x9_we), .clk(Clk), .Q(x9));  // open: clr
  Register #(.width(32)) register_10 (.D(Data), .en(x10_we), .clk(Clk), .Q(x10));  // open: clr
  Register #(.width(32)) register_11 (.D(Data), .en(x11_we), .clk(Clk), .Q(x11));  // open: clr
  Register #(.width(32)) register_12 (.D(Data), .en(x12_we), .clk(Clk), .Q(x12));  // open: clr
  Register #(.width(32)) register_13 (.D(Data), .en(x13_we), .clk(Clk), .Q(x13));  // open: clr
  Register #(.width(32)) register_14 (.D(Data), .en(x14_we), .clk(Clk), .Q(x14));  // open: clr
  Register #(.width(32)) register_15 (.D(Data), .en(x15_we), .clk(Clk), .Q(x15));  // open: clr
  Register #(.width(32)) register_16 (.D(Data), .en(x16_we), .clk(Clk), .Q(x16));  // open: clr
  Register #(.width(32)) register_17 (.D(Data), .en(x17_we), .clk(Clk), .Q(x17));  // open: clr
  Register #(.width(32)) register_18 (.D(Data), .en(x18_we), .clk(Clk), .Q(x18));  // open: clr
  Register #(.width(32)) register_19 (.D(Data), .en(x19_we), .clk(Clk), .Q(x19));  // open: clr
  Register #(.width(32)) register_20 (.D(Data), .en(x20_we), .clk(Clk), .Q(x20));  // open: clr
  Register #(.width(32)) register_21 (.D(Data), .en(x21_we), .clk(Clk), .Q(x21));  // open: clr
  Register #(.width(32)) register_22 (.D(Data), .en(x22_we), .clk(Clk), .Q(x22));  // open: clr
  Register #(.width(32)) register_23 (.D(Data), .en(x23_we), .clk(Clk), .Q(x23));  // open: clr
  Register #(.width(32)) register_24 (.D(Data), .en(x24_we), .clk(Clk), .Q(x24));  // open: clr
  Register #(.width(32)) register_25 (.D(Data), .en(x25_we), .clk(Clk), .Q(x25));  // open: clr
  Register #(.width(32)) register_26 (.D(Data), .en(x26_we), .clk(Clk), .Q(x26));  // open: clr
  Register #(.width(32)) register_27 (.D(Data), .en(x27_we), .clk(Clk), .Q(x27));  // open: clr
  Register #(.width(32)) register_28 (.D(Data), .en(x28_we), .clk(Clk), .Q(x28));  // open: clr
  Register #(.width(32)) register_29 (.D(Data), .en(x29_we), .clk(Clk), .Q(x29));  // open: clr
  Register #(.width(32)) register_30 (.D(Data), .en(x30_we), .clk(Clk), .Q(x30));  // open: clr
  Register #(.width(32)) register_31 (.D(Data), .en(x31_we), .clk(Clk), .Q(TEST_x31Data));  // open: clr
  Multiplexer #(.select(5), .width(32)) multiplexer_1 (
    .in0({32{1'b0}}), .in1(x1), .in2(x2), .in3(x3), .in4(x4), .in5(x5), .in6(x6), .in7(x7), .in8(x8),
    .in9(x9), .in10(x10), .in11(x11), .in12(x12), .in13(x13), .in14(x14), .in15(x15), .in16(x16), .in17(x17),
    .in18(x18), .in19(x19), .in20(x20), .in21(x21), .in22(x22), .in23(x23), .in24(x24), .in25(x25),
    .in26(x26), .in27(x27), .in28(x28), .in29(x29), .in30(x30), .in31(TEST_x31Data), .out(DataA_t),
    .sel(Rs1Addr));
  Multiplexer #(.select(5), .width(32)) multiplexer_2 (
    .in0({32{1'b0}}), .in1(x1), .in2(x2), .in3(x3), .in4(x4), .in5(x5), .in6(x6), .in7(x7), .in8(x8),
    .in9(x9), .in10(x10), .in11(x11), .in12(x12), .in13(x13), .in14(x14), .in15(x15), .in16(x16), .in17(x17),
    .in18(x18), .in19(x19), .in20(x20), .in21(x21), .in22(x22), .in23(x23), .in24(x24), .in25(x25),
    .in26(x26), .in27(x27), .in28(x28), .in29(x29), .in30(x30), .in31(TEST_x31Data), .out(DataB_t),
    .sel(Rs2Addr));
  RegXORComparitor regxorcomparitor_1 (.A(Rs1Addr), .B(RdAddr), .EQ(rs1_EQ_rdi));
  Multiplexer #(.width(32)) multiplexer_3 (.in0(DataA_t), .in1(Data), .out(DataA), .sel(and_1_out));
  and and_1 (and_1_out, rs1_EQ_rdi, WriteEnable, rd_not_zero);
  RegXORComparitor regxorcomparitor_2 (.A(Rs2Addr), .B(RdAddr), .EQ(rs2_EQ_rdi));
  Multiplexer #(.width(32)) multiplexer_4 (.in0(DataB_t), .in1(Data), .out(DataB), .sel(and_2_out));
  and and_2 (and_2_out, rs2_EQ_rdi, WriteEnable, rd_not_zero);
  or or_1 (rd_not_zero, RdAddr[0], RdAddr[1], RdAddr[2], RdAddr[3], RdAddr[4]);

  // Other names for the same wires on the sheet: DataAOut[31:0] = DataA; DataBOut[31:0] = DataB; rd[4:0] = RdAddr;
  //   rs1[4:0] = Rs1Addr; rs2[4:0] = Rs2Addr; we_in = WriteEnable; x31[31:0] = TEST_x31Data

  // Notes on the sheet:
  //   Write-Back to Decode RAW Data Hazard.
  //   Expose x31 for test results
endmodule

module LoadAligner (
  input  [31:0] MemAddr,
  input  [31:0] Data,
  input  [2:0] ByteSel,
  output [31:0] Out0
);

  wire and_3_out, B, missAlign;
  wire [4:3] shamt;
  wire [31:0] lb, lbu, lh, lhu, shiftedData;

  // Probe on Data
  // Probe on ByteSel
  // Probe on MemAddr[1:0]
  // Probe on MemAddr
  and and_1 (B, ~ByteSel[1], ~ByteSel[2]);  // AND_Gate
  and and_2 (missAlign, MemAddr[0], ~MemAddr[1], ByteSel[1], ~ByteSel[2]);  // AND_Gate
  and and_3 (and_3_out, ~MemAddr[0], B, ~ByteSel[2]);  // AND_Gate
  or or_1 (shamt[3], and_3_out, missAlign);
  and and_4 (shamt[4], ~MemAddr[1], ~ByteSel[2], ~missAlign);  // AND_Gate
  Shifter #(.shift("lr"), .width(32)) shifter_1 (.in(Data), .\dist ({shamt, 3'b000}), .out(shiftedData));
  // Probe on {shamt, 3'b000}
  // Probe on shiftedData
  assign lb = {{24{shiftedData[7]}}, shiftedData[7:0]};  // Bit_Extender bit_extender_1
  assign lbu = {{24{1'b0}}, shiftedData[7:0]};  // Bit_Extender bit_extender_2
  assign lh = {{16{shiftedData[15]}}, shiftedData[15:0]};  // Bit_Extender bit_extender_3
  assign lhu = {{16{1'b0}}, shiftedData[15:0]};  // Bit_Extender bit_extender_4
  Multiplexer #(.select(3), .width(32)) multiplexer_1 (
    .in0(lb), .in1(lbu), .in2(lh), .in3(lhu), .in4(Data), .out(Out0), .sel(ByteSel));  // open: in5, in6, in7
  // Probe on ByteSel

  // Other names for the same wires on the sheet: H = ByteSel[1]; W = ByteSel[2]; dataIn[31:0] = Data;
  //   AddrOffset[1:0] = MemAddr[1:0]; offset0 = MemAddr[0]; offset1 = MemAddr[1]

  // Notes on the sheet:
  //   Signed Byte = 000
  //   Unsigned Byte = 001
  //   Signed Half Word = 010
  //   Unsigned Half Word = 011
  //   Full Word = 100
  //   Shift data by address offset amount
endmodule

module StoreMaskGenerator (
  input  [1:0] AddrOffset,
  input  [2:0] ByteSel,
  output [3:0] OutMask
);

  wire A0_AND_B, A0_OR_H, A1_AND_NOT_A0_AND_B, A1_XOR_A0, and_5_out, and_6_out, and_7_out, and_8_out,
       and_9_out, B, B_OR_H, NOT_A0, NOT_A0_AND_H, NOT_A1, or_3_out, or_4_out, or_5_out;

  not not_1 (NOT_A0, AddrOffset[0]);
  not not_2 (NOT_A1, AddrOffset[1]);
  and and_1 (B, ~ByteSel[1], ~ByteSel[2]);  // AND_Gate
  and and_2 (NOT_A0_AND_H, NOT_A0, ByteSel[1]);
  and and_3 (A0_AND_B, AddrOffset[0], B);
  or or_1 (B_OR_H, B, ByteSel[1]);
  and and_4 (A1_AND_NOT_A0_AND_B, AddrOffset[1], NOT_A0, B);
  xor xor_1 (A1_XOR_A0, AddrOffset[1], AddrOffset[0]);
  or or_2 (A0_OR_H, ByteSel[1], AddrOffset[0]);
  and and_5 (and_5_out, AddrOffset[1], or_3_out);
  or or_3 (or_3_out, A0_AND_B, ByteSel[1]);
  and and_6 (and_6_out, A1_XOR_A0, ByteSel[1]);
  and and_7 (and_7_out, NOT_A1, or_4_out);
  or or_4 (or_4_out, NOT_A0_AND_H, A0_AND_B);
  and and_8 (and_8_out, NOT_A1, and_9_out);
  and and_9 (and_9_out, NOT_A0, B_OR_H);
  or or_5 (or_5_out, A1_AND_NOT_A0_AND_B, and_6_out);
  or or_6 (OutMask[1], or_5_out, ByteSel[2]);
  or or_7 (OutMask[3], and_8_out, ByteSel[2]);
  or or_8 (OutMask[0], and_5_out, ByteSel[2]);
  or or_9 (OutMask[2], and_7_out, A0_OR_H, ByteSel[2]);

  // Other names for the same wires on the sheet: A0 = AddrOffset[0]; A1 = AddrOffset[1]; H = ByteSel[1];
  //   W = ByteSel[2]

  // Notes on the sheet:
  //   Mask[0] = W OR (A1 AND (A0 AND B OR H))
  //   Mask[1] = W OR (A1 AND ~A0 AND B) OR (H AND (A1 XOR A0))
  //   Mask[2] = W OR (~A1 AND (A0 AND B OR ~A0 AND H))
  //   Mask[3] = W OR (~A1 AND (~A0 AND B OR H))
endmodule

module StoreAligner (
  input  [31:0] MemAddr,
  input  [31:0] Data,
  input  [2:0] ByteSel,
  output [31:0] DataOut,
  output [3:0] MaskOut
);

  wire and_3_out, B, missAlign;
  wire [4:3] shamt;

  // Probe on MemAddr[1:0]
  // Probe on MemAddr
  // Probe on Data
  // Probe on ByteSel
  and and_1 (B, ~ByteSel[1], ~ByteSel[2]);  // AND_Gate
  and and_2 (missAlign, MemAddr[0], ~MemAddr[1], ByteSel[1], ~ByteSel[2]);  // AND_Gate
  and and_3 (and_3_out, ~MemAddr[0], B, ~ByteSel[2]);  // AND_Gate
  or or_1 (shamt[3], and_3_out, missAlign);
  and and_4 (shamt[4], ~MemAddr[1], ~ByteSel[2], ~missAlign);  // AND_Gate
  // Probe on MaskOut
  StoreMaskGenerator storemaskgenerator_1 (.AddrOffset(MemAddr[1:0]), .ByteSel(ByteSel), .OutMask(MaskOut));
  // Probe on {shamt, 3'b000}
  // Probe on DataOut
  Shifter #(.width(32)) shifter_1 (.in(Data), .\dist ({shamt, 3'b000}), .out(DataOut));

  // Other names for the same wires on the sheet: dataIn[31:0] = Data; AddrOffset[1:0] = MemAddr[1:0];
  //   offset0 = MemAddr[0]; offset1 = MemAddr[1]; MemByteSel[2:0] = ByteSel; H = ByteSel[1]; W = ByteSel[2];
  //   shiftedData[31:0] = DataOut; StoreMask[3:0] = MaskOut

  // Notes on the sheet:
  //   Shift data by address offset amount
endmodule

module IMem (
  input  [31:0] PC,
  output [31:0] Inst
);

  // Probe on PC
  ROM #(.addrWidth(10), .dataWidth(32)) IMem (.addr(PC[11:2]), .data(Inst));
  // Probe on Inst

  // Notes on the sheet:
  //   contents of IMem (hex, n*v repeats v):
  //   93 113 193 213 293 4000093 2a00113 20a023 4000093 a183 2219a63 a00213 1400293 1013 26313 500213
  //   500293 520463 140006f 0 0 100f93 6f fff00f93 ffdff06f
endmodule

module DMem (
  input  [31:0] MemAddr,
  input  MemWrite,
  input  MemRead,
  input  [3:0] StoreMast,
  input  clk,
  input  [31:0] WriteData,
  output [31:0] MemOut
);

  // Probe on MemAddr
  RAM #(.addrWidth(10), .asyncread("true"), .byteenables("byteEnables"), .dataWidth(32)) DMem (
    .addr(MemAddr[11:2]), .we(MemWrite), .oe(MemRead), .clk(clk), .din(WriteData), .dout(MemOut),
    .be3(StoreMast[3]), .be2(StoreMast[2]), .be1(StoreMast[1]), .be0(StoreMast[0]));
  // Probe on WriteData
  // Probe on MemOut

  // Other names for the same wires on the sheet: AddrOffset[1:0] = MemAddr[1:0]; MemWriteData[31:0] = WriteData;
  //   StoreMask[3:0] = StoreMast; SysClk = clk

  // Notes on the sheet:
  //   MEM - Memory
endmodule

module RegXORComparitor (
  input  [4:0] A,
  input  [4:0] B,
  output EQ
);

  wire [4:0] xor_1_out;

  assign xor_1_out = A ^ B;  // XOR_Gate xor_1, 5 bits wide
  and and_1 (EQ, ~xor_1_out[0], ~xor_1_out[1], ~xor_1_out[2], ~xor_1_out[3], ~xor_1_out[4]);  // AND_Gate
endmodule

module CSR (
  input  [11:0] CSRAddr,
  input  [31:0] RDataA,
  input  [4:0] rdi,
  input  [4:0] uimm,
  input  inst_valid,
  input  [3:0] CSRCtl,
  input  clk,
  output [31:0] DataOut,
  output [31:0] test0,
  output [31:0] test1,
  output [31:0] cycle,
  output [31:0] instret,
  output [31:0] ttime
);

  wire and_5_out, and_6_out, and_7_out, and_8_out, and_9_out, and_10_out, and_11_out, and_12_out, and_13_out,
       and_14_out, and_15_out, and_16_out, and_17_out, and_18_out, and_19_out, is_cycle, is_htest0,
       is_htest1, is_instret, is_mcause, is_medeleg, is_mepc, is_mideleg, is_mstatus, is_mtvec, is_rdi_zero,
       is_satp, is_scause, is_sepc, is_source_zero, is_sscratch, is_sstatus, is_stval, is_stvec, is_ttime,
       is_uimm_zero, nand_1_out, WE;
  wire [31:0] and_3_out, bit_extender_1_out, cycle_inc, cycle_out, DataIn, htest0_out, htest1_out,
       instret_inc, instret_out, mcause_out, medeleg_out, mepc_out, mideleg_out, mstatus_out, mtvec_out,
       multiplexer_2_out, multiplexer_3_out, multiplexer_4_out, NewData, or_1_out, ram_1_dout, register_4_q,
       register_5_q, register_6_q, register_7_q, register_8_q, register_9_q, register_10_q, register_11_q,
       register_12_q, register_13_q, register_14_q, register_15_q, register_16_q, satp_out, scause_out,
       sepc_out, sscratch_out, sstatus_out, stval_out, stvec_out, ttime_out;

  // Probe on CSRAddr
  // Probe on CSRCtl
  and and_1 (is_rdi_zero, ~rdi[0], ~rdi[1], ~rdi[2], ~rdi[3], ~rdi[4]);  // AND_Gate
  and and_2 (is_uimm_zero, ~uimm[0], ~uimm[1], ~uimm[2], ~uimm[3], ~uimm[4]);  // AND_Gate
  Multiplexer multiplexer_1 (.in0(is_rdi_zero), .in1(is_uimm_zero), .out(is_source_zero), .sel(CSRCtl[2]));
  Multiplexer #(.width(32)) multiplexer_2 (.in0({32{1'b0}}), .in1(32'h1), .out(multiplexer_2_out), .sel(inst_valid));
  Adder #(.width(32)) adder_1 (.a(32'h1), .b(cycle), .out(cycle_inc));  // open: cin, cout
  Register #(.width(32)) register_1 (.D({32{1'b0}}), .en(1'b1), .clk(clk), .Q(ttime));  // open: clr
  // Probe on uimm
  CSRAddrEQ csraddreq_1 (.A(CSRAddr), .B(12'hc00), .EQ(is_cycle));
  Register #(.width(32)) register_2 (.D(multiplexer_3_out), .en(1'b1), .clk(clk), .Q(cycle));  // open: clr
  Multiplexer #(.width(32)) multiplexer_3 (.in0(cycle_inc), .in1(NewData), .out(multiplexer_3_out), .sel(is_cycle));
  CSRAddrEQ csraddreq_2 (.A(CSRAddr), .B(12'hc01), .EQ(is_ttime));
  CSRAddrEQ csraddreq_3 (.A(CSRAddr), .B(12'hc02), .EQ(is_instret));
  Register #(.width(32)) register_3 (.D(multiplexer_4_out), .en(1'b1), .clk(clk), .Q(instret));  // open: clr
  Multiplexer #(.width(32)) multiplexer_4 (.in0(instret_inc), .in1(NewData), .out(multiplexer_4_out), .sel(is_instret));
  Adder #(.width(32)) adder_2 (.a(multiplexer_2_out), .b(instret), .out(instret_inc));  // open: cin, cout
  // Probe on RDataA
  assign bit_extender_1_out = {{27{1'b0}}, uimm};  // Bit_Extender bit_extender_1
  assign or_1_out = DataIn | DataOut;  // OR_Gate or_1, 32 bits wide
  assign and_3_out = ~DataIn & DataOut;  // AND_Gate and_3, 32 bits wide
  Multiplexer #(.width(32)) multiplexer_5 (.in0({32{1'b0}}), .in1(ttime), .out(ttime_out), .sel(is_ttime));
  Multiplexer #(.width(32)) multiplexer_6 (.in0(RDataA), .in1(bit_extender_1_out), .out(DataIn), .sel(CSRCtl[2]));
  // Probe on DataIn
  Multiplexer #(.select(2), .width(32)) multiplexer_7 (
    .in1(DataIn), .in2(or_1_out), .in3(and_3_out), .out(NewData), .sel(CSRCtl[1:0]));  // open: in0
  nand nand_1 (nand_1_out, CSRCtl[1], is_source_zero);
  and and_4 (WE, nand_1_out, CSRCtl[3]);
  Multiplexer #(.width(32)) multiplexer_8 (.in0({32{1'b0}}), .in1(cycle), .out(cycle_out), .sel(is_cycle));
  // Probe on NewData
  Multiplexer #(.width(32)) multiplexer_9 (.in0({32{1'b0}}), .in1(instret), .out(instret_out), .sel(is_instret));
  Register #(.width(32)) register_4 (.D(NewData), .en(and_5_out), .clk(clk), .Q(register_4_q));  // open: clr
  and and_5 (and_5_out, is_mstatus, WE);
  Register #(.width(32)) register_5 (.D(NewData), .en(and_6_out), .clk(clk), .Q(register_5_q));  // open: clr
  and and_6 (and_6_out, is_medeleg, WE);
  Register #(.width(32)) register_6 (.D(NewData), .en(and_7_out), .clk(clk), .Q(register_6_q));  // open: clr
  and and_7 (and_7_out, is_mideleg, WE);
  Register #(.width(32)) register_7 (.D(NewData), .en(and_8_out), .clk(clk), .Q(register_7_q));  // open: clr
  and and_8 (and_8_out, is_mtvec, WE);
  Register #(.width(32)) register_8 (.D(NewData), .en(and_9_out), .clk(clk), .Q(register_8_q));  // open: clr
  and and_9 (and_9_out, is_mepc, WE);
  Register #(.width(32)) register_9 (.D(NewData), .en(and_10_out), .clk(clk), .Q(register_9_q));  // open: clr
  and and_10 (and_10_out, is_mcause, WE);
  CSRAddrEQ csraddreq_4 (.A(CSRAddr), .B(12'h300), .EQ(is_mstatus));
  CSRAddrEQ csraddreq_5 (.A(CSRAddr), .B(12'h302), .EQ(is_medeleg));
  CSRAddrEQ csraddreq_6 (.A(CSRAddr), .B(12'h303), .EQ(is_mideleg));
  CSRAddrEQ csraddreq_7 (.A(CSRAddr), .B(12'h305), .EQ(is_mtvec));
  CSRAddrEQ csraddreq_8 (.A(CSRAddr), .B(12'h341), .EQ(is_mepc));
  CSRAddrEQ csraddreq_9 (.A(CSRAddr), .B(12'h342), .EQ(is_mcause));
  Multiplexer #(.width(32)) multiplexer_10 (.in0({32{1'b0}}), .in1(register_4_q), .out(mstatus_out), .sel(is_mstatus));
  Multiplexer #(.width(32)) multiplexer_11 (.in0({32{1'b0}}), .in1(register_5_q), .out(medeleg_out), .sel(is_medeleg));
  Multiplexer #(.width(32)) multiplexer_12 (.in0({32{1'b0}}), .in1(register_6_q), .out(mideleg_out), .sel(is_mideleg));
  Multiplexer #(.width(32)) multiplexer_13 (.in0({32{1'b0}}), .in1(register_7_q), .out(mtvec_out), .sel(is_mtvec));
  Multiplexer #(.width(32)) multiplexer_14 (.in0({32{1'b0}}), .in1(register_8_q), .out(mepc_out), .sel(is_mepc));
  Multiplexer #(.width(32)) multiplexer_15 (.in0({32{1'b0}}), .in1(register_9_q), .out(mcause_out), .sel(is_mcause));
  Register #(.width(32)) register_10 (.D(NewData), .en(and_11_out), .clk(clk), .Q(register_10_q));  // open: clr
  and and_11 (and_11_out, is_sstatus, WE);
  Register #(.width(32)) register_11 (.D(NewData), .en(and_12_out), .clk(clk), .Q(register_11_q));  // open: clr
  and and_12 (and_12_out, is_stvec, WE);
  Register #(.width(32)) register_12 (.D(NewData), .en(and_13_out), .clk(clk), .Q(register_12_q));  // open: clr
  and and_13 (and_13_out, is_sscratch, WE);
  Register #(.width(32)) register_13 (.D(NewData), .en(and_14_out), .clk(clk), .Q(register_13_q));  // open: clr
  and and_14 (and_14_out, is_sepc, WE);
  Register #(.width(32)) register_14 (.D(NewData), .en(and_15_out), .clk(clk), .Q(register_14_q));  // open: clr
  and and_15 (and_15_out, is_scause, WE);
  Register #(.width(32)) register_15 (.D(NewData), .en(and_16_out), .clk(clk), .Q(register_15_q));  // open: clr
  and and_16 (and_16_out, is_stval, WE);
  Register #(.width(32)) register_16 (.D(NewData), .en(and_17_out), .clk(clk), .Q(register_16_q));  // open: clr
  and and_17 (and_17_out, is_satp, WE);
  CSRAddrEQ csraddreq_10 (.A(CSRAddr), .B(12'h100), .EQ(is_sstatus));
  CSRAddrEQ csraddreq_11 (.A(CSRAddr), .B(12'h105), .EQ(is_stvec));
  CSRAddrEQ csraddreq_12 (.A(CSRAddr), .B(12'h140), .EQ(is_sscratch));
  CSRAddrEQ csraddreq_13 (.A(CSRAddr), .B(12'h141), .EQ(is_sepc));
  CSRAddrEQ csraddreq_14 (.A(CSRAddr), .B(12'h142), .EQ(is_scause));
  CSRAddrEQ csraddreq_15 (.A(CSRAddr), .B(12'h143), .EQ(is_stval));
  CSRAddrEQ csraddreq_16 (.A(CSRAddr), .B(12'h180), .EQ(is_satp));
  Multiplexer #(.width(32)) multiplexer_16 (.in0({32{1'b0}}), .in1(register_10_q), .out(sstatus_out), .sel(is_sstatus));
  Multiplexer #(.width(32)) multiplexer_17 (.in0({32{1'b0}}), .in1(register_11_q), .out(stvec_out), .sel(is_stvec));
  Multiplexer #(.width(32)) multiplexer_18 (
    .in0({32{1'b0}}), .in1(register_12_q), .out(sscratch_out), .sel(is_sscratch));
  Multiplexer #(.width(32)) multiplexer_19 (.in0({32{1'b0}}), .in1(register_13_q), .out(sepc_out), .sel(is_sepc));
  Multiplexer #(.width(32)) multiplexer_20 (.in0({32{1'b0}}), .in1(register_14_q), .out(scause_out), .sel(is_scause));
  Multiplexer #(.width(32)) multiplexer_21 (.in0({32{1'b0}}), .in1(register_15_q), .out(stval_out), .sel(is_stval));
  Multiplexer #(.width(32)) multiplexer_22 (.in0({32{1'b0}}), .in1(register_16_q), .out(satp_out), .sel(is_satp));
  // Probe on DataOut
  assign DataOut = cycle_out | ttime_out | instret_out | mstatus_out | medeleg_out | mideleg_out | mtvec_out | mepc_out | mcause_out | sstatus_out | stvec_out | sscratch_out | sepc_out | scause_out | stval_out | satp_out | htest0_out | htest1_out;  // OR_Gate or_2, 32 bits wide
  and and_18 (and_18_out, is_htest0, WE);
  and and_19 (and_19_out, is_htest1, WE);
  CSRAddrEQ csraddreq_17 (.A(CSRAddr), .B(12'h7c0), .EQ(is_htest0));
  Register #(.width(32)) register_17 (.D(NewData), .en(and_18_out), .clk(clk), .Q(test0));  // open: clr
  CSRAddrEQ csraddreq_18 (.A(CSRAddr), .B(12'h7c1), .EQ(is_htest1));
  Register #(.width(32)) register_18 (.D(NewData), .en(and_19_out), .clk(clk), .Q(test1));  // open: clr
  Multiplexer #(.width(32)) multiplexer_23 (.in0({32{1'b0}}), .in1(test1), .out(htest1_out), .sel(is_htest1));
  Multiplexer #(.width(32)) multiplexer_24 (.in0({32{1'b0}}), .in1(test0), .out(htest0_out), .sel(is_htest0));
  RAM #(.addrWidth(12), .dataWidth(32)) ram_1 (
    .addr(CSRAddr), .we(WE), .oe(1'b1), .clk(clk), .din(NewData), .dout(ram_1_dout));

  // Other names for the same wires on the sheet: C_cycle_out[31:0] = cycle; C_htest0_out[31:0] = test0;
  //   C_htest1_out[31:0] = test1; C_instret_out[31:0] = instret; C_ttime_out[31:0] = ttime; csr_op[1:0] = CSRCtl[1:0];
  //   is_clear_or_set = CSRCtl[1]; is_csr_uimm = CSRCtl[2]; is_csr_active = CSRCtl[3]

  // Notes on the sheet:
  //   TODO: TIME INPUT
  //   default incremented value if valid
  //   cycle
  //   time
  //   instret
  //   write value if incoming address matches instret
  //   mideleg
  //   mtvec
  //   mepc
  //   mcause
  //   mstatus
  //   medeleg
  //   stval
  //   satp
  //   sstatus
  //   stvec
  //   sscratch
  //   sepc
  //   scause
  //   htest0
  //   htest1
endmodule

module CSRAddrEQ (
  input  [11:0] A,
  input  [11:0] B,
  output EQ
);

  wire [11:0] xor_1_out;

  assign xor_1_out = A ^ B;  // XOR_Gate xor_1, 12 bits wide
  and and_1 (EQ, ~xor_1_out[0], ~xor_1_out[1], ~xor_1_out[2], ~xor_1_out[3], ~xor_1_out[4], ~xor_1_out[5], ~xor_1_out[6], ~xor_1_out[7], ~xor_1_out[8], ~xor_1_out[9], ~xor_1_out[10], ~xor_1_out[11]);  // AND_Gate
endmodule
