// Logisim project RiskVMuxDemux.circ as structural Verilog: 5 circuits, main circuit Mux2to1_1Bit
module Mux2to1_1Bit (
  input  In_A,
  input  Sel,
  input  In_B,
  output Out_Y
);

  wire and_1_out, and_2_out, not_1_out;

  and and_1 (and_1_out, In_A, not_1_out);
  not not_1 (not_1_out, Sel);
  and and_2 (and_2_out, In_B, Sel);
  or or_1 (Out_Y, and_1_out, and_2_out);
endmodule

module Mux2to1_32Bit (
  input  [31:0] In0,
  input  [31:0] In1,
  input  Sel,
  output [31:0] Out_Y
);

  wire [31:0] and_1_out, and_2_out, bit_extender_1_out, not_1_out;

  assign bit_extender_1_out = {{31{Sel}}, Sel};  // Bit_Extender bit_extender_1
  assign not_1_out = ~bit_extender_1_out;  // NOT_Gate not_1, 32 bits wide
  assign and_1_out = In0 & not_1_out;  // AND_Gate and_1, 32 bits wide
  assign and_2_out = In1 & bit_extender_1_out;  // AND_Gate and_2, 32 bits wide
  assign Out_Y = and_1_out | and_2_out;  // OR_Gate or_1, 32 bits wide
endmodule

module Mux4to1_32Bit (
  input  [31:0] In0,
  input  [31:0] In1,
  input  [31:0] In2,
  input  [31:0] In3,
  input  [1:0] Sel,
  output [31:0] Out_Y
);

  wire [31:0] mux2to1_32bit_1_out_y, mux2to1_32bit_2_out_y;

  Mux2to1_32Bit mux2to1_32bit_1 (.In0(In0), .In1(In1), .Sel(Sel[0]), .Out_Y(mux2to1_32bit_1_out_y));
  Mux2to1_32Bit mux2to1_32bit_2 (.In0(In2), .In1(In3), .Sel(Sel[0]), .Out_Y(mux2to1_32bit_2_out_y));
  Mux2to1_32Bit mux2to1_32bit_3 (.In0(mux2to1_32bit_1_out_y), .In1(mux2to1_32bit_2_out_y), .Sel(Sel[1]), .Out_Y(Out_Y));
endmodule

module DeMux1to2_32Bit (
  input  [31:0] In0,
  input  Sel,
  output [31:0] Out0,
  output [31:0] Out1
);

  wire [31:0] bit_extender_1_out, not_1_out;

  assign bit_extender_1_out = {{31{Sel}}, Sel};  // Bit_Extender bit_extender_1
  assign not_1_out = ~bit_extender_1_out;  // NOT_Gate not_1, 32 bits wide
  assign Out0 = In0 & not_1_out;  // AND_Gate and_1, 32 bits wide
  assign Out1 = In0 & bit_extender_1_out;  // AND_Gate and_2, 32 bits wide
endmodule

module DeMux1to4_32Bit (
  input  [31:0] In0,
  input  [1:0] Sel,
  output [31:0] Out0,
  output [31:0] Out1,
  output [31:0] Out2,
  output [31:0] Out3
);

  wire [31:0] demux1to2_32bit_1_out0, demux1to2_32bit_1_out1;

  DeMux1to2_32Bit demux1to2_32bit_1 (
    .In0(In0), .Sel(Sel[1]), .Out0(demux1to2_32bit_1_out0), .Out1(demux1to2_32bit_1_out1));
  DeMux1to2_32Bit demux1to2_32bit_2 (.In0(demux1to2_32bit_1_out0), .Sel(Sel[0]), .Out0(Out0), .Out1(Out1));
  DeMux1to2_32Bit demux1to2_32bit_3 (.In0(demux1to2_32bit_1_out1), .Sel(Sel[0]), .Out0(Out2), .Out1(Out3));
endmodule
