// Logisim project RiskVPipelineRegs.circ as structural Verilog: 11 circuits, main circuit PipelineReg32Bit
module PipelineReg32Bit (
  input  [31:0] DataIn,
  input  WE,
  input  FLUSH,
  input  clk,
  output [31:0] DataOut
);

  wire or_1_out;
  wire [31:0] multiplexer_1_out;

  // Probe on multiplexer_1_out
  Multiplexer #(.width(32)) multiplexer_1 (.in0(DataIn), .in1({32{1'b0}}), .out(multiplexer_1_out), .sel(FLUSH));
  or or_1 (or_1_out, WE, FLUSH);
  Register #(.width(32)) register_1 (.D(multiplexer_1_out), .en(or_1_out), .clk(clk), .Q(DataOut));  // open: clr
  // Probe on DataOut

  // Other names for the same wires on the sheet: data[31:0] = DataIn
endmodule

module PipelineReg5Bit (
  input  [4:0] DataIn,
  input  WE,
  input  FLUSH,
  input  clk,
  output [4:0] DataOut
);

  wire or_1_out;
  wire [4:0] multiplexer_1_out;

  // Probe on multiplexer_1_out
  Multiplexer #(.width(5)) multiplexer_1 (.in0(DataIn), .in1({5{1'b0}}), .out(multiplexer_1_out), .sel(FLUSH));
  or or_1 (or_1_out, WE, FLUSH);
  Register #(.width(5)) register_1 (.D(multiplexer_1_out), .en(or_1_out), .clk(clk), .Q(DataOut));  // open: clr
  // Probe on DataOut

  // Other names for the same wires on the sheet: data[4:0] = DataIn
endmodule

module PipelineReg1Bit (
  input  DataIn,
  input  WE,
  input  FLUSH,
  input  clk,
  output DataOut
);

  wire multiplexer_1_out, or_1_out;

  // Probe on multiplexer_1_out
  Multiplexer multiplexer_1 (.in0(DataIn), .in1(1'b0), .out(multiplexer_1_out), .sel(FLUSH));
  or or_1 (or_1_out, WE, FLUSH);
  Register #(.width(1)) register_1 (.D(multiplexer_1_out), .en(or_1_out), .clk(clk), .Q(DataOut));  // open: clr
  // Probe on DataOut

  // Other names for the same wires on the sheet: data = DataIn
endmodule

module PipelineReg3Bit (
  input  [2:0] DataIn,
  input  WE,
  input  FLUSH,
  input  clk,
  output [2:0] DataOut
);

  wire or_1_out;
  wire [2:0] multiplexer_1_out;

  // Probe on multiplexer_1_out
  Multiplexer #(.width(3)) multiplexer_1 (.in0(DataIn), .in1(3'b000), .out(multiplexer_1_out), .sel(FLUSH));
  or or_1 (or_1_out, WE, FLUSH);
  Register #(.width(3)) register_1 (.D(multiplexer_1_out), .en(or_1_out), .clk(clk), .Q(DataOut));  // open: clr
  // Probe on DataOut

  // Other names for the same wires on the sheet: data[2:0] = DataIn
endmodule

module PipelineReg2Bit (
  input  [1:0] DataIn,
  input  WE,
  input  FLUSH,
  input  clk,
  output [1:0] DataOut
);

  wire or_1_out;
  wire [1:0] multiplexer_1_out;

  // Probe on multiplexer_1_out
  Multiplexer #(.width(2)) multiplexer_1 (.in0(DataIn), .in1(2'b00), .out(multiplexer_1_out), .sel(FLUSH));
  or or_1 (or_1_out, WE, FLUSH);
  Register #(.width(2)) register_1 (.D(multiplexer_1_out), .en(or_1_out), .clk(clk), .Q(DataOut));  // open: clr
  // Probe on DataOut

  // Other names for the same wires on the sheet: data[1:0] = DataIn
endmodule

module PipelineReg4Bit (
  input  [3:0] DataIn,
  input  WE,
  input  FLUSH,
  input  clk,
  output [3:0] DataOut
);

  wire or_1_out;
  wire [3:0] multiplexer_1_out;

  // Probe on multiplexer_1_out
  Multiplexer #(.width(4)) multiplexer_1 (.in0(DataIn), .in1(4'b0000), .out(multiplexer_1_out), .sel(FLUSH));
  or or_1 (or_1_out, WE, FLUSH);
  Register #(.width(4)) register_1 (.D(multiplexer_1_out), .en(or_1_out), .clk(clk), .Q(DataOut));  // open: clr
  // Probe on DataOut

  // Other names for the same wires on the sheet: data[3:0] = DataIn
endmodule

module PipelineReg12Bit (
  input  [11:0] DataIn,
  input  WE,
  input  FLUSH,
  input  clk,
  output [11:0] DataOut
);

  wire or_1_out;
  wire [11:0] multiplexer_1_out;

  // Probe on multiplexer_1_out
  Multiplexer #(.width(12)) multiplexer_1 (.in0(DataIn), .in1({12{1'b0}}), .out(multiplexer_1_out), .sel(FLUSH));
  or or_1 (or_1_out, WE, FLUSH);
  Register #(.width(12)) register_1 (.D(multiplexer_1_out), .en(or_1_out), .clk(clk), .Q(DataOut));  // open: clr
  // Probe on DataOut

  // Other names for the same wires on the sheet: data[11:0] = DataIn
endmodule

module IF_ID (
  input  [31:0] Inst,
  input  [31:0] PC,
  input  [31:0] PCPlus4,
  input  IF_ID_WE,
  input  IF_ID_FLUSH,
  input  SysClk,
  output [31:0] IF_ID_Inst,
  output [31:0] IF_ID_PC,
  output [31:0] IF_ID_PC_4,
  output IF_ID_valid
);

  wire and_1_out;

  and and_1 (and_1_out, IF_ID_WE, ~IF_ID_FLUSH);  // AND_Gate
  PipelineReg32Bit ID_ID_INST (.DataIn(Inst), .WE(IF_ID_WE), .FLUSH(IF_ID_FLUSH), .clk(SysClk), .DataOut(IF_ID_Inst));
  PipelineReg32Bit pipelinereg32bit_1 (.DataIn(PC), .WE(IF_ID_WE), .clk(SysClk), .DataOut(IF_ID_PC));  // open: FLUSH
  PipelineReg32Bit pipelinereg32bit_2 (
    .DataIn(PCPlus4), .WE(IF_ID_WE), .clk(SysClk), .DataOut(IF_ID_PC_4));  // open: FLUSH
  PipelineReg1Bit pipelinereg1bit_1 (
    .DataIn(and_1_out), .WE(IF_ID_WE), .clk(SysClk), .DataOut(IF_ID_valid));  // open: FLUSH

  // Notes on the sheet:
  //   IF_ID
endmodule

module ID_EX (
  input  [31:0] RDataA,
  input  [31:0] RDataB,
  input  [31:0] Imm,
  input  ASel,
  input  BSel,
  input  [4:0] ALUSel,
  input  [4:0] BrSel,
  input  MemRead,
  input  MemWrite,
  input  [2:0] MemByteSel,
  input  RegWEn,
  input  [1:0] WBSel,
  input  [11:0] CSRAddr,
  input  [3:0] CSRCtl,
  input  ecall,
  input  ebreak,
  input  [4:0] rdi,
  input  [4:0] rs1,
  input  [4:0] rs2,
  input  [31:0] IF_ID_PC,
  input  [31:0] IF_ID_PC_4,
  input  ID_EX_FLUSH,
  input  IF_ID_valid,
  input  SysClk,
  output [31:0] ID_EX_RDataA,
  output [31:0] ID_EX_RDataB,
  output [31:0] ID_EX_Imm,
  output ID_EX_ASel,
  output ID_EX_BSel,
  output [4:0] ID_EX_ALUSel,
  output [4:0] ID_EX_BrSel,
  output ID_EX_MemRead,
  output ID_EX_MemWrite,
  output [2:0] ID_EX_MemByteSel,
  output ID_EX_RegWEn,
  output [1:0] ID_EX_WBSel,
  output [11:0] ID_EX_CSRAddr,
  output [3:0] ID_EX_CSRCtl,
  output ID_EX_ecall,
  output ID_EX_ebreak,
  output [4:0] ID_EX_rdi,
  output [4:0] ID_EX_rs1,
  output [4:0] ID_EX_rs2,
  output [31:0] ID_EX_PC,
  output [31:0] ID_EX_PC_4,
  output ID_EX_valid
);

  wire and_1_out;

  and and_1 (and_1_out, IF_ID_valid, ~ID_EX_FLUSH);  // AND_Gate
  PipelineReg32Bit pipelinereg32bit_1 (
    .DataIn(RDataA), .WE(1'b1), .FLUSH(ID_EX_FLUSH), .clk(SysClk), .DataOut(ID_EX_RDataA));
  PipelineReg32Bit pipelinereg32bit_2 (
    .DataIn(RDataB), .WE(1'b1), .FLUSH(ID_EX_FLUSH), .clk(SysClk), .DataOut(ID_EX_RDataB));
  PipelineReg32Bit pipelinereg32bit_3 (.DataIn(Imm), .WE(1'b1), .FLUSH(ID_EX_FLUSH), .clk(SysClk), .DataOut(ID_EX_Imm));
  PipelineReg1Bit pipelinereg1bit_1 (.DataIn(ASel), .WE(1'b1), .FLUSH(ID_EX_FLUSH), .clk(SysClk), .DataOut(ID_EX_ASel));
  PipelineReg1Bit pipelinereg1bit_2 (.DataIn(BSel), .WE(1'b1), .FLUSH(ID_EX_FLUSH), .clk(SysClk), .DataOut(ID_EX_BSel));
  PipelineReg5Bit pipelinereg5bit_1 (
    .DataIn(ALUSel), .WE(1'b1), .FLUSH(ID_EX_FLUSH), .clk(SysClk), .DataOut(ID_EX_ALUSel));
  PipelineReg5Bit pipelinereg5bit_2 (
    .DataIn(BrSel), .WE(1'b1), .FLUSH(ID_EX_FLUSH), .clk(SysClk), .DataOut(ID_EX_BrSel));
  PipelineReg1Bit pipelinereg1bit_3 (
    .DataIn(MemRead), .WE(1'b1), .FLUSH(ID_EX_FLUSH), .clk(SysClk), .DataOut(ID_EX_MemRead));
  PipelineReg1Bit pipelinereg1bit_4 (
    .DataIn(MemWrite), .WE(1'b1), .FLUSH(ID_EX_FLUSH), .clk(SysClk), .DataOut(ID_EX_MemWrite));
  PipelineReg3Bit pipelinereg3bit_1 (
    .DataIn(MemByteSel), .WE(1'b1), .FLUSH(ID_EX_FLUSH), .clk(SysClk), .DataOut(ID_EX_MemByteSel));
  PipelineReg1Bit pipelinereg1bit_5 (
    .DataIn(RegWEn), .WE(1'b1), .FLUSH(ID_EX_FLUSH), .clk(SysClk), .DataOut(ID_EX_RegWEn));
  PipelineReg2Bit pipelinereg2bit_1 (
    .DataIn(WBSel), .WE(1'b1), .FLUSH(ID_EX_FLUSH), .clk(SysClk), .DataOut(ID_EX_WBSel));
  PipelineReg12Bit pipelinereg12bit_1 (
    .DataIn(CSRAddr), .WE(1'b1), .FLUSH(ID_EX_FLUSH), .clk(SysClk), .DataOut(ID_EX_CSRAddr));
  PipelineReg4Bit pipelinereg4bit_1 (
    .DataIn(CSRCtl), .WE(1'b1), .FLUSH(ID_EX_FLUSH), .clk(SysClk), .DataOut(ID_EX_CSRCtl));
  PipelineReg1Bit pipelinereg1bit_6 (
    .DataIn(ecall), .WE(1'b1), .FLUSH(ID_EX_FLUSH), .clk(SysClk), .DataOut(ID_EX_ecall));
  PipelineReg1Bit pipelinereg1bit_7 (
    .DataIn(ebreak), .WE(1'b1), .FLUSH(ID_EX_FLUSH), .clk(SysClk), .DataOut(ID_EX_ebreak));
  PipelineReg5Bit pipelinereg5bit_3 (.DataIn(rdi), .WE(1'b1), .FLUSH(ID_EX_FLUSH), .clk(SysClk), .DataOut(ID_EX_rdi));
  PipelineReg5Bit pipelinereg5bit_4 (.DataIn(rs1), .WE(1'b1), .FLUSH(ID_EX_FLUSH), .clk(SysClk), .DataOut(ID_EX_rs1));
  PipelineReg5Bit pipelinereg5bit_5 (.DataIn(rs2), .WE(1'b1), .FLUSH(ID_EX_FLUSH), .clk(SysClk), .DataOut(ID_EX_rs2));
  PipelineReg32Bit pipelinereg32bit_4 (.DataIn(IF_ID_PC), .WE(1'b1), .clk(SysClk), .DataOut(ID_EX_PC));  // open: FLUSH
  PipelineReg32Bit pipelinereg32bit_5 (
    .DataIn(IF_ID_PC_4), .WE(1'b1), .clk(SysClk), .DataOut(ID_EX_PC_4));  // open: FLUSH
  PipelineReg1Bit pipelinereg1bit_8 (
    .DataIn(and_1_out), .WE(1'b1), .clk(SysClk), .DataOut(ID_EX_valid));  // open: FLUSH

  // Notes on the sheet:
  //   ID_EX
endmodule

module EX_MEM (
  input  [31:0] ALUOut,
  input  [31:0] RDataB,
  input  [31:0] RDataA,
  input  ID_EX_MemRead,
  input  ID_EX_MemWrite,
  input  [2:0] ID_EX_MemByteSel,
  input  ID_EX_RegWEn,
  input  [1:0] ID_EX_WBSel,
  input  [11:0] ID_EX_CSRAddr,
  input  [3:0] ID_EX_CSRCtl,
  input  ID_EX_ecall,
  input  ID_EX_ebreak,
  input  [4:0] ID_EX_rdi,
  input  [4:0] ID_EX_rs1,
  input  [31:0] ID_EX_PC,
  input  [31:0] ID_EX_PC_4,
  input  ID_EX_valid,
  input  SysClk,
  output [31:0] EX_MEM_ALUOut,
  output [31:0] EX_MEM_RDataB,
  output [31:0] EX_MEM_RDataA,
  output EX_MEM_MemRead,
  output EX_MEM_MemWrite,
  output [2:0] EX_MEM_MemByteSel,
  output EX_MEM_RegWEn,
  output [1:0] EX_MEM_WBSel,
  output [11:0] EX_MEM_CSRAddr,
  output [3:0] EX_MEM_CSRCtl,
  output EX_MEM_ecall,
  output EX_MEM_ebreak,
  output [4:0] EX_MEM_rdi,
  output [4:0] EX_MEM_rs1,
  output [31:0] EX_MEM_PC,
  output [31:0] EX_MEM_PC_4,
  output EX_MEM_valid
);

  PipelineReg32Bit pipelinereg32bit_1 (.DataIn(ALUOut), .WE(1'b1), .FLUSH(1'b0), .clk(SysClk), .DataOut(EX_MEM_ALUOut));
  PipelineReg32Bit pipelinereg32bit_2 (.DataIn(RDataB), .WE(1'b1), .FLUSH(1'b0), .clk(SysClk), .DataOut(EX_MEM_RDataB));
  PipelineReg32Bit pipelinereg32bit_3 (.DataIn(RDataA), .WE(1'b1), .FLUSH(1'b0), .clk(SysClk), .DataOut(EX_MEM_RDataA));
  PipelineReg1Bit pipelinereg1bit_1 (
    .DataIn(ID_EX_MemRead), .WE(1'b1), .FLUSH(1'b0), .clk(SysClk), .DataOut(EX_MEM_MemRead));
  PipelineReg1Bit pipelinereg1bit_2 (
    .DataIn(ID_EX_MemWrite), .WE(1'b1), .FLUSH(1'b0), .clk(SysClk), .DataOut(EX_MEM_MemWrite));
  PipelineReg3Bit pipelinereg3bit_1 (
    .DataIn(ID_EX_MemByteSel), .WE(1'b1), .FLUSH(1'b0), .clk(SysClk), .DataOut(EX_MEM_MemByteSel));
  PipelineReg1Bit pipelinereg1bit_3 (
    .DataIn(ID_EX_RegWEn), .WE(1'b1), .FLUSH(1'b0), .clk(SysClk), .DataOut(EX_MEM_RegWEn));
  PipelineReg2Bit pipelinereg2bit_1 (
    .DataIn(ID_EX_WBSel), .WE(1'b1), .FLUSH(1'b0), .clk(SysClk), .DataOut(EX_MEM_WBSel));
  PipelineReg12Bit pipelinereg12bit_1 (
    .DataIn(ID_EX_CSRAddr), .WE(1'b1), .FLUSH(1'b0), .clk(SysClk), .DataOut(EX_MEM_CSRAddr));
  PipelineReg4Bit pipelinereg4bit_1 (
    .DataIn(ID_EX_CSRCtl), .WE(1'b1), .FLUSH(1'b0), .clk(SysClk), .DataOut(EX_MEM_CSRCtl));
  PipelineReg1Bit pipelinereg1bit_4 (
    .DataIn(ID_EX_ecall), .WE(1'b1), .FLUSH(1'b0), .clk(SysClk), .DataOut(EX_MEM_ecall));
  PipelineReg1Bit pipelinereg1bit_5 (
    .DataIn(ID_EX_ebreak), .WE(1'b1), .FLUSH(1'b0), .clk(SysClk), .DataOut(EX_MEM_ebreak));
  PipelineReg5Bit pipelinereg5bit_1 (.DataIn(ID_EX_rdi), .WE(1'b1), .FLUSH(1'b0), .clk(SysClk), .DataOut(EX_MEM_rdi));
  PipelineReg5Bit pipelinereg5bit_2 (.DataIn(ID_EX_rs1), .WE(1'b1), .FLUSH(1'b0), .clk(SysClk), .DataOut(EX_MEM_rs1));
  PipelineReg32Bit pipelinereg32bit_4 (.DataIn(ID_EX_PC), .WE(1'b1), .clk(SysClk), .DataOut(EX_MEM_PC));  // open: FLUSH
  PipelineReg32Bit pipelinereg32bit_5 (
    .DataIn(ID_EX_PC_4), .WE(1'b1), .clk(SysClk), .DataOut(EX_MEM_PC_4));  // open: FLUSH
  PipelineReg1Bit pipelinereg1bit_6 (
    .DataIn(ID_EX_valid), .WE(1'b1), .clk(SysClk), .DataOut(EX_MEM_valid));  // open: FLUSH

  // Other names for the same wires on the sheet: ID_EX_RDataA[31:0] = RDataA; ID_EX_RDataB[31:0] = RDataB
endmodule

module MEM_WB (
  input  [31:0] MemData,
  input  [31:0] CSROut,
  input  [31:0] EX_MEM_ALUOut,
  input  EX_MEM_RegWEn,
  input  [1:0] EX_MEM_WBSel,
  input  EX_MEM_ecall,
  input  EX_MEM_ebreak,
  input  [4:0] EX_MEM_rdi,
  input  [31:0] EX_MEM_PC,
  input  [31:0] EX_MEM_PC_4,
  input  EX_MEM_valid,
  input  SysClk,
  output [31:0] MEM_WB_MemOut,
  output [31:0] MEM_WB_CSROut,
  output [31:0] MEM_WB_ALUOut,
  output MEM_WB_RegWEn,
  output [1:0] MEM_WB_WBSel,
  output MEM_WB_ecall,
  output MEM_WB_ebreak,
  output [4:0] MEM_WB_rdi,
  output [31:0] MEM_WB_PC,
  output [31:0] MEM_WB_PC_4,
  output MEM_WB_valid
);

  PipelineReg32Bit pipelinereg32bit_1 (
    .DataIn(MemData), .WE(1'b1), .FLUSH(1'b0), .clk(SysClk), .DataOut(MEM_WB_MemOut));
  PipelineReg32Bit pipelinereg32bit_2 (
    .DataIn(EX_MEM_ALUOut), .WE(1'b1), .FLUSH(1'b0), .clk(SysClk), .DataOut(MEM_WB_ALUOut));
  PipelineReg1Bit pipelinereg1bit_1 (
    .DataIn(EX_MEM_RegWEn), .WE(1'b1), .FLUSH(1'b0), .clk(SysClk), .DataOut(MEM_WB_RegWEn));
  PipelineReg2Bit pipelinereg2bit_1 (
    .DataIn(EX_MEM_WBSel), .WE(1'b1), .FLUSH(1'b0), .clk(SysClk), .DataOut(MEM_WB_WBSel));
  PipelineReg1Bit pipelinereg1bit_2 (
    .DataIn(EX_MEM_ecall), .WE(1'b1), .FLUSH(1'b0), .clk(SysClk), .DataOut(MEM_WB_ecall));
  PipelineReg1Bit pipelinereg1bit_3 (
    .DataIn(EX_MEM_ebreak), .WE(1'b1), .FLUSH(1'b0), .clk(SysClk), .DataOut(MEM_WB_ebreak));
  PipelineReg5Bit pipelinereg5bit_1 (.DataIn(EX_MEM_rdi), .WE(1'b1), .FLUSH(1'b0), .clk(SysClk), .DataOut(MEM_WB_rdi));
  PipelineReg32Bit pipelinereg32bit_3 (
    .DataIn(EX_MEM_PC), .WE(1'b1), .clk(SysClk), .DataOut(MEM_WB_PC));  // open: FLUSH
  PipelineReg32Bit pipelinereg32bit_4 (
    .DataIn(EX_MEM_PC_4), .WE(1'b1), .clk(SysClk), .DataOut(MEM_WB_PC_4));  // open: FLUSH
  PipelineReg32Bit pipelinereg32bit_5 (
    .DataIn(CSROut), .WE(1'b1), .clk(SysClk), .DataOut(MEM_WB_CSROut));  // open: FLUSH
  PipelineReg1Bit pipelinereg1bit_4 (
    .DataIn(EX_MEM_valid), .WE(1'b1), .clk(SysClk), .DataOut(MEM_WB_valid));  // open: FLUSH

  // Notes on the sheet:
  //   MEM_WB
endmodule
