// Logisim project WriteBackController_DOCS.circ as structural Verilog: 1 circuit, main circuit WriteBackControl
module WriteBackControl (
  input  [31:0] ALUOut,
  input  [31:0] MemOut,
  input  [31:0] PCPlus4,
  input  [1:0] WBSel,
  output [31:0] OutData
);

  // Probe on OutData
  Multiplexer #(.select(2), .width(32)) multiplexer_1 (
    .in0(ALUOut), .in1(MemOut), .in2(PCPlus4), .out(OutData), .sel(WBSel));  // open: in3
  // Probe on WBSel

  // Other names for the same wires on the sheet: MemOutAligned[31:0] = MemOut; RegWBData[31:0] = OutData

  // Notes on the sheet:
  //   00 = ALU
  //   01 = Mem
  //   11 = PCPlus4
endmodule
