// Logisim project Adder.circ as structural Verilog: 3 circuits, main circuit HalfAdder
module HalfAdder (
  input  In0,
  input  In1,
  output OutSum,
  output OutCarry
);

  xor xor_1 (OutSum, In0, In1);
  and and_1 (OutCarry, In0, In1);
endmodule

module FullAdder (
  input  Cin,
  input  A,
  input  B,
  output Sum,
  output Cout
);

  wire and_1_out, and_2_out, and_3_out, xor_1_out;

  xor xor_1 (xor_1_out, B, A);
  and and_1 (and_1_out, A, Cin);
  and and_2 (and_2_out, Cin, B);
  and and_3 (and_3_out, A, B);
  xor xor_2 (Sum, xor_1_out, Cin);
  or or_1 (Cout, and_1_out, and_2_out, and_3_out);
endmodule

module AdderSub32 (
  input  Cin,
  input  Sub,
  input  [31:0] B,
  input  [31:0] A,
  output [31:0] Sum,
  output Cout
);

  wire B0, B1, B2, B3, B4, B5, B6, B7, B8, B9, B10, B11, B12, B13, B14, B15, B16, B17, B18, B19, B20, B21,
       B22, B23, B24, B25, B26, B27, B28, B29, B30, B31, fulladder_1_cout, fulladder_2_cout,
       fulladder_3_cout, fulladder_4_cout, fulladder_5_cout, fulladder_6_cout, fulladder_7_cout,
       fulladder_8_cout, fulladder_9_cout, fulladder_10_cout, fulladder_11_cout, fulladder_12_cout,
       fulladder_13_cout, fulladder_14_cout, fulladder_15_cout, fulladder_16_cout, fulladder_17_cout,
       fulladder_18_cout, fulladder_19_cout, fulladder_20_cout, fulladder_21_cout, fulladder_22_cout,
       fulladder_23_cout, fulladder_24_cout, fulladder_25_cout, fulladder_26_cout, fulladder_27_cout,
       fulladder_28_cout, fulladder_29_cout, fulladder_30_cout, fulladder_31_cout;
  wire [31:0] bit_extender_1_out;

  assign bit_extender_1_out = {{31{Sub}}, Sub};  // Bit_Extender bit_extender_1
  assign {B31, B30, B29, B28, B27, B26, B25, B24, B23, B22, B21, B20, B19, B18, B17, B16, B15, B14, B13, B12, B11, B10, B9, B8, B7, B6, B5, B4, B3, B2, B1, B0} = bit_extender_1_out ^ B;  // XOR_Gate xor_1, 32 bits wide
  FullAdder fulladder_1 (.Cin(Cin), .A(A[0]), .B(B0), .Sum(Sum[0]), .Cout(fulladder_1_cout));
  FullAdder fulladder_2 (.Cin(fulladder_1_cout), .A(A[1]), .B(B1), .Sum(Sum[1]), .Cout(fulladder_2_cout));
  FullAdder fulladder_3 (.Cin(fulladder_2_cout), .A(A[2]), .B(B2), .Sum(Sum[2]), .Cout(fulladder_3_cout));
  FullAdder fulladder_4 (.Cin(fulladder_3_cout), .A(A[3]), .B(B3), .Sum(Sum[3]), .Cout(fulladder_4_cout));
  FullAdder fulladder_5 (.Cin(fulladder_4_cout), .A(A[4]), .B(B4), .Sum(Sum[4]), .Cout(fulladder_5_cout));
  FullAdder fulladder_6 (.Cin(fulladder_5_cout), .A(A[5]), .B(B5), .Sum(Sum[5]), .Cout(fulladder_6_cout));
  FullAdder fulladder_7 (.Cin(fulladder_6_cout), .A(A[6]), .B(B6), .Sum(Sum[6]), .Cout(fulladder_7_cout));
  FullAdder fulladder_8 (.Cin(fulladder_7_cout), .A(A[7]), .B(B7), .Sum(Sum[7]), .Cout(fulladder_8_cout));
  FullAdder fulladder_9 (.Cin(fulladder_8_cout), .A(A[8]), .B(B8), .Sum(Sum[8]), .Cout(fulladder_9_cout));
  FullAdder fulladder_10 (.Cin(fulladder_9_cout), .A(A[9]), .B(B9), .Sum(Sum[9]), .Cout(fulladder_10_cout));
  FullAdder fulladder_11 (.Cin(fulladder_10_cout), .A(A[10]), .B(B10), .Sum(Sum[10]), .Cout(fulladder_11_cout));
  FullAdder fulladder_12 (.Cin(fulladder_11_cout), .A(A[11]), .B(B11), .Sum(Sum[11]), .Cout(fulladder_12_cout));
  FullAdder fulladder_13 (.Cin(fulladder_12_cout), .A(A[12]), .B(B12), .Sum(Sum[12]), .Cout(fulladder_13_cout));
  FullAdder fulladder_14 (.Cin(fulladder_13_cout), .A(A[13]), .B(B13), .Sum(Sum[13]), .Cout(fulladder_14_cout));
  FullAdder fulladder_15 (.Cin(fulladder_14_cout), .A(A[14]), .B(B14), .Sum(Sum[14]), .Cout(fulladder_15_cout));
  FullAdder fulladder_16 (.Cin(fulladder_15_cout), .A(A[15]), .B(B15), .Sum(Sum[15]), .Cout(fulladder_16_cout));
  FullAdder fulladder_17 (.Cin(fulladder_16_cout), .A(A[16]), .B(B16), .Sum(Sum[16]), .Cout(fulladder_17_cout));
  FullAdder fulladder_18 (.Cin(fulladder_17_cout), .A(A[17]), .B(B17), .Sum(Sum[17]), .Cout(fulladder_18_cout));
  FullAdder fulladder_19 (.Cin(fulladder_18_cout), .A(A[18]), .B(B18), .Sum(Sum[18]), .Cout(fulladder_19_cout));
  FullAdder fulladder_20 (.Cin(fulladder_19_cout), .A(A[19]), .B(B19), .Sum(Sum[19]), .Cout(fulladder_20_cout));
  FullAdder fulladder_21 (.Cin(fulladder_20_cout), .A(A[20]), .B(B20), .Sum(Sum[20]), .Cout(fulladder_21_cout));
  FullAdder fulladder_22 (.Cin(fulladder_21_cout), .A(A[21]), .B(B21), .Sum(Sum[21]), .Cout(fulladder_22_cout));
  FullAdder fulladder_23 (.Cin(fulladder_22_cout), .A(A[22]), .B(B22), .Sum(Sum[22]), .Cout(fulladder_23_cout));
  FullAdder fulladder_24 (.Cin(fulladder_23_cout), .A(A[23]), .B(B23), .Sum(Sum[23]), .Cout(fulladder_24_cout));
  FullAdder fulladder_25 (.Cin(fulladder_24_cout), .A(A[24]), .B(B24), .Sum(Sum[24]), .Cout(fulladder_25_cout));
  FullAdder fulladder_26 (.Cin(fulladder_25_cout), .A(A[25]), .B(B25), .Sum(Sum[25]), .Cout(fulladder_26_cout));
  FullAdder fulladder_27 (.Cin(fulladder_26_cout), .A(A[26]), .B(B26), .Sum(Sum[26]), .Cout(fulladder_27_cout));
  FullAdder fulladder_28 (.Cin(fulladder_27_cout), .A(A[27]), .B(B27), .Sum(Sum[27]), .Cout(fulladder_28_cout));
  FullAdder fulladder_29 (.Cin(fulladder_28_cout), .A(A[28]), .B(B28), .Sum(Sum[28]), .Cout(fulladder_29_cout));
  FullAdder fulladder_30 (.Cin(fulladder_29_cout), .A(A[29]), .B(B29), .Sum(Sum[29]), .Cout(fulladder_30_cout));
  FullAdder fulladder_31 (.Cin(fulladder_30_cout), .A(A[30]), .B(B30), .Sum(Sum[30]), .Cout(fulladder_31_cout));
  FullAdder fulladder_32 (.Cin(fulladder_31_cout), .A(A[31]), .B(B31), .Sum(Sum[31]), .Cout(Cout));
endmodule
