// Logisim project Arith.circ as structural Verilog: 3 circuits, main circuit WordLevelComparator
module WordLevelComparator (
  input  [31:0] InSum,
  input  InCout,
  input  ASignIn,
  input  BSignIn,
  output EQ,
  output LTU,
  output LTS
);

  wire or_1_out, xor_1_out;

  not not_1 (LTU, InCout);
  xor xor_1 (xor_1_out, ASignIn, BSignIn);
  Multiplexer multiplexer_1 (.in0(LTU), .in1(ASignIn), .out(LTS), .sel(xor_1_out));
  or or_1 (or_1_out, InSum[0], InSum[1], InSum[2], InSum[3], InSum[4], InSum[5], InSum[6], InSum[7], InSum[8], InSum[9], InSum[10], InSum[11], InSum[12], InSum[13], InSum[14], InSum[15], InSum[16], InSum[17], InSum[18], InSum[19], InSum[20], InSum[21], InSum[22], InSum[23], InSum[24], InSum[25], InSum[26], InSum[27], InSum[28], InSum[29], InSum[30], InSum[31]);
  not not_2 (EQ, or_1_out);
endmodule

module BranchSelector (
  input  EQ,
  input  LTS,
  input  LTU,
  input  [2:0] func3,
  output TakeBranch
);

  wire not_1_out, not_2_out, not_3_out;

  not not_1 (not_1_out, EQ);
  not not_2 (not_2_out, LTS);
  not not_3 (not_3_out, LTU);
  Multiplexer #(.select(3)) multiplexer_1 (
    .in0(EQ), .in1(not_1_out), .in2(1'b0), .in3(1'b0), .in4(LTS), .in5(not_2_out), .in6(LTU),
    .in7(not_3_out), .out(TakeBranch), .sel(func3));
endmodule

module BitwiseLogicUnit (
  input  [31:0] B,
  input  [31:0] A,
  input  [2:0] func3,
  output [31:0] Out0
);

  wire [31:0] and_1_out, or_1_out, xor_1_out;

  assign xor_1_out = A ^ B;  // XOR_Gate xor_1, 32 bits wide
  assign or_1_out = B | A;  // OR_Gate or_1, 32 bits wide
  assign and_1_out = B & A;  // AND_Gate and_1, 32 bits wide
  Multiplexer #(.select(2), .width(32)) multiplexer_1 (
    .in0(xor_1_out), .in1({32{1'b0}}), .in2(or_1_out), .in3(and_1_out), .out(Out0), .sel(func3[1:0]));
endmodule
