// Logisim project CSRRegister.circ as structural Verilog: 1 circuit, main circuit CSR
module CSR (
  input  [11:0] CSRAddr,
  input  [31:0] RDataA,
  input  [4:0] rdi,
  input  [4:0] uimm,
  input  [3:0] CSRCtl,
  input  clk,
  output [31:0] DataOut
);

  wire is_rdi_zero, is_source_zero, is_uimm_zero, nand_1_out, WE;
  wire [31:0] and_3_out, bit_extender_1_out, DataIn, NewData, or_1_out;

  and and_1 (is_rdi_zero, ~rdi[0], ~rdi[1], ~rdi[2], ~rdi[3], ~rdi[4]);  // AND_Gate
  and and_2 (is_uimm_zero, ~uimm[0], ~uimm[1], ~uimm[2], ~uimm[3], ~uimm[4]);  // AND_Gate
  Multiplexer multiplexer_1 (.in0(is_rdi_zero), .in1(is_uimm_zero), .out(is_source_zero), .sel(CSRCtl[2]));
  assign bit_extender_1_out = {{27{1'b0}}, uimm};  // Bit_Extender bit_extender_1
  assign or_1_out = DataIn | DataOut;  // OR_Gate or_1, 32 bits wide
  assign and_3_out = ~DataIn & DataOut;  // AND_Gate and_3, 32 bits wide
  Multiplexer #(.width(32)) multiplexer_2 (.in0(RDataA), .in1(bit_extender_1_out), .out(DataIn), .sel(CSRCtl[2]));
  Multiplexer #(.select(2), .width(32)) multiplexer_3 (
    .in1(DataIn), .in2(or_1_out), .in3(and_3_out), .out(NewData), .sel(CSRCtl[1:0]));  // open: in0
  nand nand_1 (nand_1_out, CSRCtl[1], is_source_zero);
  and and_4 (WE, nand_1_out, CSRCtl[3]);
  RAM #(.addrWidth(12), .dataWidth(32)) ram_1 (
    .addr(CSRAddr), .we(WE), .oe(1'b1), .clk(clk), .din(NewData), .dout(DataOut));

  // Other names for the same wires on the sheet: csr_op[1:0] = CSRCtl[1:0]; is_clear_or_set = CSRCtl[1];
  //   is_csr_uimm = CSRCtl[2]; is_csr_active = CSRCtl[3]
endmodule
