// Logisim project EncoderDecoder.circ as structural Verilog: 5 circuits, main circuit Decoder2to4
module Decoder2to4 (
  input  [1:0] In0,
  input  E,
  output Out3,
  output Out2,
  output Out1,
  output Out0
);

  wire Bit0_bar_t, Bit1_bar_t;

  not not_1 (Bit0_bar_t, In0[0]);
  not not_2 (Bit1_bar_t, In0[1]);
  and and_1 (Out3, In0[1], E, In0[0]);
  and and_2 (Out2, In0[1], E, Bit0_bar_t);
  and and_3 (Out1, In0[0], E, Bit1_bar_t);
  and and_4 (Out0, Bit0_bar_t, E, Bit1_bar_t);

  // Other names for the same wires on the sheet: E_t = E; Bit0_t = In0[0]; Bit1_t = In0[1]
endmodule

module Decoder3to8 (
  input  [2:0] In0,
  output Out7,
  output Out6,
  output Out5,
  output Out4,
  output Out3,
  output Out2,
  output Out1,
  output Out0
);

  wire not_1_out;

  not not_1 (not_1_out, In0[2]);
  Decoder2to4 decoder2to4_1 (.In0(In0[1:0]), .E(not_1_out), .Out3(Out3), .Out2(Out2), .Out1(Out1), .Out0(Out0));
  Decoder2to4 decoder2to4_2 (.In0(In0[1:0]), .E(In0[2]), .Out3(Out7), .Out2(Out6), .Out1(Out5), .Out0(Out4));
endmodule

module Encoder4to2_Simple (
  input  In0,
  input  In1,
  input  In2,
  input  In3,
  output [1:0] Out_Y
);

  or or_1 (Out_Y[0], In1, In3);
  or or_2 (Out_Y[1], In3, In2);
endmodule

module Encoder4to2 (
  input  In0,
  input  In1,
  input  In2,
  input  In3,
  output [1:0] Out_Y,
  output V
);

  wire and_1_out, not_1_out;

  not not_1 (not_1_out, In2);
  or or_1 (V, In0, In1, In2, In3);
  and and_1 (and_1_out, In1, not_1_out);
  or or_2 (Out_Y[0], and_1_out, In3);
  or or_3 (Out_Y[1], In2, In3);

  // Other names for the same wires on the sheet: Valid_t = V
endmodule

module Encoder8to3 (
  input  In0,
  input  In1,
  input  In2,
  input  In3,
  input  In4,
  input  In5,
  input  In6,
  input  In7,
  output [2:0] Out_Y,
  output V
);

  wire High_Bit0, High_Bit1, Low_Bit0, Low_Bit1, Low_V;

  Encoder4to2 Low (.In0(In0), .In1(In1), .In2(In2), .In3(In3), .Out_Y({Low_Bit1, Low_Bit0}), .V(Low_V));
  Encoder4to2 High (.In0(In4), .In1(In5), .In2(In6), .In3(In7), .Out_Y({High_Bit1, High_Bit0}), .V(Out_Y[2]));
  Multiplexer multiplexer_1 (.in0(Low_Bit1), .in1(High_Bit1), .out(Out_Y[1]), .sel(Out_Y[2]));
  Multiplexer multiplexer_2 (.in0(Low_Bit0), .in1(High_Bit0), .out(Out_Y[0]), .sel(Out_Y[2]));
  or or_1 (V, Out_Y[2], Low_V);

  // Other names for the same wires on the sheet: Out0_t = Out_Y[0]; Out1_t = Out_Y[1]; High_V = Out_Y[2]; Valid_t = V
endmodule
