// Logisim project ImmGen.circ as structural Verilog: 2 circuits, main circuit ImmGen32Bit
module ImmGen32Bit (
  input  [31:0] InstIn,
  input  [2:0] ImmSelIn,
  output [31:0] ImmOut
);

  Multiplexer #(.select(3), .width(32)) multiplexer_1 (
    .in0({{21{InstIn[31]}}, InstIn[30:20]}), .in1({{21{InstIn[31]}}, InstIn[30:25], InstIn[11:7]}),
    .in2({{20{InstIn[31]}}, InstIn[7], InstIn[30:25], InstIn[11:8], 1'b0}),
    .in3({InstIn[31:12], {12{1'b0}}}),
    .in4({{12{InstIn[31]}}, InstIn[19:12], InstIn[20], InstIn[30:21], 1'b0}), .out(ImmOut), .sel(ImmSelIn));  // open: in5, in6, in7

  // Other names for the same wires on the sheet: BType[31:1] = {{20{InstIn[31]}}, InstIn[7], InstIn[30:25], InstIn[11:8]};
  //   Ins8 = InstIn[8]; SType[31:0] = {{21{InstIn[31]}}, InstIn[30:25], InstIn[11:7]}; Ins9 = InstIn[9];
  //   Ins10 = InstIn[10]; Ins11 = InstIn[11]; Ins7 = InstIn[7]; ImmSel[2:0] = ImmSelIn; Ins0 = InstIn[0];
  //   Ins1 = InstIn[1]; Ins2 = InstIn[2]; Ins3 = InstIn[3]; Ins4 = InstIn[4]; Ins5 = InstIn[5]; Ins6 = InstIn[6];
  //   Ins21 = InstIn[21]; IType[31:0] = {{21{InstIn[31]}}, InstIn[30:20]};
  //   JType[31:1] = {{12{InstIn[31]}}, InstIn[19:12], InstIn[20], InstIn[30:21]}; UType[31:12] = InstIn[31:12];
  //   Ins22 = InstIn[22]; Ins23 = InstIn[23]; Ins24 = InstIn[24]; Ins25 = InstIn[25]; Ins26 = InstIn[26];
  //   Ins27 = InstIn[27]; Ins28 = InstIn[28]; Ins29 = InstIn[29]; Ins30 = InstIn[30]; Ins20 = InstIn[20];
  //   Ins12 = InstIn[12]; Ins13 = InstIn[13]; Ins14 = InstIn[14]; Ins15 = InstIn[15]; Ins16 = InstIn[16];
  //   Ins17 = InstIn[17]; Ins18 = InstIn[18]; Ins19 = InstIn[19]; Ins31 = InstIn[31]

  // Notes on the sheet:
  //   I-Type
  //   S-Type
  //   B-Type
  //   U-Type
  //   J-Type
endmodule

module ImmGen64Bit (
  input  [31:0] InstIn,
  input  [2:0] ImmSelIn,
  output [63:0] ImmOut
);

  Multiplexer #(.select(3), .width(64)) multiplexer_1 (
    .in0({{53{InstIn[31]}}, InstIn[30:20]}), .in1({{53{InstIn[31]}}, InstIn[30:25], InstIn[11:7]}),
    .in2({{52{InstIn[31]}}, InstIn[7], InstIn[30:25], InstIn[11:8], 1'b0}),
    .in3({{33{InstIn[31]}}, InstIn[30:12], {12{1'b0}}}),
    .in4({{44{InstIn[31]}}, InstIn[19:12], InstIn[20], InstIn[30:21], 1'b0}), .out(ImmOut), .sel(ImmSelIn));  // open: in5, in6, in7

  // Other names for the same wires on the sheet: BType[63:1] = {{52{InstIn[31]}}, InstIn[7], InstIn[30:25], InstIn[11:8]};
  //   Ins8 = InstIn[8]; SType[63:0] = {{53{InstIn[31]}}, InstIn[30:25], InstIn[11:7]}; Ins9 = InstIn[9];
  //   Ins10 = InstIn[10]; Ins11 = InstIn[11]; Ins7 = InstIn[7]; ImmSel[2:0] = ImmSelIn; Ins0 = InstIn[0];
  //   Ins1 = InstIn[1]; Ins2 = InstIn[2]; Ins3 = InstIn[3]; Ins4 = InstIn[4]; Ins5 = InstIn[5]; Ins6 = InstIn[6];
  //   Ins21 = InstIn[21]; IType[63:0] = {{53{InstIn[31]}}, InstIn[30:20]};
  //   JType[63:1] = {{44{InstIn[31]}}, InstIn[19:12], InstIn[20], InstIn[30:21]};
  //   UType[63:12] = {{33{InstIn[31]}}, InstIn[30:12]}; Ins22 = InstIn[22]; Ins23 = InstIn[23]; Ins24 = InstIn[24];
  //   Ins25 = InstIn[25]; Ins26 = InstIn[26]; Ins27 = InstIn[27]; Ins28 = InstIn[28]; Ins29 = InstIn[29];
  //   Ins30 = InstIn[30]; Ins20 = InstIn[20]; Ins12 = InstIn[12]; Ins13 = InstIn[13]; Ins14 = InstIn[14];
  //   Ins15 = InstIn[15]; Ins16 = InstIn[16]; Ins17 = InstIn[17]; Ins18 = InstIn[18]; Ins19 = InstIn[19];
  //   Ins31 = InstIn[31]

  // Notes on the sheet:
  //   I-Type
  //   S-Type
  //   B-Type
  //   U-Type
  //   J-Type
endmodule
