// Logisim project Memory.circ as structural Verilog: 7 circuits, main circuit D_Latch
module Register_32Bit (
  input  [31:0] D,
  input  WE,
  input  Clk,
  output [31:0] out_4
);

  Register_16Bit register_16bit_1 (.D(D[15:0]), .WE(WE), .Clk(Clk), .out_4(out_4[15:0]));
  Register_16Bit register_16bit_2 (.D(D[31:16]), .WE(WE), .Clk(Clk), .out_4(out_4[31:16]));

  // Other names for the same wires on the sheet: Clk_t = Clk; B15_0_t[15:0] = D[15:0]; B31_16_t[15:0] = D[31:16];
  //   B15_0_Q_t[15:0] = out_4[15:0]; B31_16_Q_t[15:0] = out_4[31:16]; WE_t = WE
endmodule

module Register_16Bit (
  input  [15:0] D,
  input  WE,
  input  Clk,
  output [15:0] out_4
);

  Register_8Bit register_8bit_1 (.D(D[7:0]), .WE(WE), .Clk(Clk), .Q(out_4[7:0]));
  Register_8Bit register_8bit_2 (.D(D[15:8]), .WE(WE), .Clk(Clk), .Q(out_4[15:8]));

  // Other names for the same wires on the sheet: Clk_t = Clk; B7_0_t[7:0] = D[7:0]; B15_8_t[7:0] = D[15:8];
  //   B7_0_Q_t[7:0] = out_4[7:0]; B15_8_Q_t[7:0] = out_4[15:8]; WE_t = WE
endmodule

module Register_8Bit (
  input  [7:0] D,
  input  WE,
  input  Clk,
  output [7:0] Q
);

  Register_1Bit register_1bit_1 (.D(D[0]), .Clk(Clk), .WE(WE), .Q(Q[0]));  // open: Q_bar
  Register_1Bit register_1bit_2 (.D(D[1]), .Clk(Clk), .WE(WE), .Q(Q[1]));  // open: Q_bar
  Register_1Bit register_1bit_3 (.D(D[2]), .Clk(Clk), .WE(WE), .Q(Q[2]));  // open: Q_bar
  Register_1Bit register_1bit_4 (.D(D[3]), .Clk(Clk), .WE(WE), .Q(Q[3]));  // open: Q_bar
  Register_1Bit register_1bit_5 (.D(D[4]), .Clk(Clk), .WE(WE), .Q(Q[4]));  // open: Q_bar
  Register_1Bit register_1bit_6 (.D(D[5]), .Clk(Clk), .WE(WE), .Q(Q[5]));  // open: Q_bar
  Register_1Bit register_1bit_7 (.D(D[6]), .Clk(Clk), .WE(WE), .Q(Q[6]));  // open: Q_bar
  Register_1Bit register_1bit_8 (.D(D[7]), .Clk(Clk), .WE(WE), .Q(Q[7]));  // open: Q_bar

  // Other names for the same wires on the sheet: Clk_t = Clk; B0_t = D[0]; B1_t = D[1]; B2_t = D[2]; B3_t = D[3];
  //   B4_t = D[4]; B5_t = D[5]; B6_t = D[6]; B7_t = D[7]; B0_Q_t = Q[0]; B1_Q_t = Q[1]; B2_Q_t = Q[2]; B3_Q_t = Q[3];
  //   B4_Q_t = Q[4]; B5_Q_t = Q[5]; B6_Q_t = Q[6]; B7_Q_t = Q[7]; WE_t = WE

  // Notes on the sheet:
  //   D: initial=0x42
endmodule

module Register_1Bit (
  input  D,
  input  Clk,
  input  WE,
  output Q,
  output Q_bar
);

  wire multiplexer_1_out;

  Multiplexer multiplexer_1 (.in0(Q), .in1(D), .out(multiplexer_1_out), .sel(WE));
  D_FlipFlop d_flipflop_1 (.D(multiplexer_1_out), .Clk(Clk), .Q(Q), .Q_bar(Q_bar));
endmodule

module D_FlipFlop (
  input  D,
  input  Clk,
  output Q,
  output Q_bar
);

  wire Master_q, not_1_out;

  not not_1 (not_1_out, Clk);
  D_Latch Master (.D(D), .E(not_1_out), .Q(Master_q));  // open: Q_bar
  D_Latch Slave (.D(Master_q), .E(Clk), .Q(Q), .Q_bar(Q_bar));
endmodule

module D_Latch (
  input  D,
  input  E,
  output Q,
  output Q_bar
);

  wire and_1_out, and_2_out, not_1_out;

  not not_1 (not_1_out, D);
  and and_1 (and_1_out, not_1_out, E);
  and and_2 (and_2_out, E, D);
  SR_Latch sr_latch_1 (.R(and_1_out), .S(and_2_out), .Q(Q), .Q_bar(Q_bar));
endmodule

module SR_Latch (
  input  R,
  input  S,
  output Q,
  output Q_bar
);

  wire or_1_out, or_2_out;

  or or_1 (or_1_out, R, Q_bar);
  not not_1 (Q, or_1_out);
  or or_2 (or_2_out, Q, S);
  not not_2 (Q_bar, or_2_out);
endmodule
