// Logisim project UniShifter.circ as structural Verilog: 8 circuits, main circuit ShiftRot32Bit
module ShiftRot32Bit (
  input  [31:0] In0,
  input  [2:0] InCtl,
  input  [4:0] InShAmt,
  output [31:0] Out0
);

  wire and_2_out, and_3_out, not_1_out, not_2_out, or_1_out, S0_t, S1_t, S2_t, S3_t, S4_t;
  wire [31:0] and_1_out, ArithMask, ClearMask, multiplexer_1_out, multiplexer_2_out, multiplexer_3_out,
       multiplexer_4_out, or_2_out, rot1_32bit_1_out_2, rot2_32bit_1_out_2, rot4_32bit_1_out_2,
       rot8_32bit_1_out_2, rot16_32bit_1_out_2, RotOut, ShiftOut;

  // Probe on In0
  // Probe on InShAmt
  rot1_32bit rot1_32bit_1 (.in_1(In0), .out_2(rot1_32bit_1_out_2));
  Multiplexer #(.width(32)) multiplexer_1 (.in0(In0), .in1(rot1_32bit_1_out_2), .out(multiplexer_1_out), .sel(S0_t));
  ShiftDirCtl shiftdirctl_1 (.InShAmt(InShAmt), .InDir(InCtl[0]), .OutDir({S4_t, S3_t, S2_t, S1_t, S0_t}));
  Multiplexer #(.width(32)) multiplexer_2 (
    .in0(multiplexer_1_out), .in1(rot2_32bit_1_out_2), .out(multiplexer_2_out), .sel(S1_t));
  rot2_32bit rot2_32bit_1 (.in_1(multiplexer_1_out), .out_2(rot2_32bit_1_out_2));
  // Probe on {S4_t, S3_t, S2_t, S1_t, S0_t}
  rot4_32bit rot4_32bit_1 (.in_1(multiplexer_2_out), .out_2(rot4_32bit_1_out_2));
  Multiplexer #(.width(32)) multiplexer_3 (
    .in0(multiplexer_2_out), .in1(rot4_32bit_1_out_2), .out(multiplexer_3_out), .sel(S2_t));
  or or_1 (or_1_out, S0_t, S1_t, S2_t, S3_t, S4_t);
  assign and_1_out = RotOut & ClearMask;  // AND_Gate and_1, 32 bits wide
  not not_1 (not_1_out, InCtl[1]);
  Multiplexer #(.width(32)) multiplexer_4 (
    .in0(multiplexer_3_out), .in1(rot8_32bit_1_out_2), .out(multiplexer_4_out), .sel(S3_t));
  rot8_32bit rot8_32bit_1 (.in_1(multiplexer_3_out), .out_2(rot8_32bit_1_out_2));
  and and_2 (and_2_out, or_1_out, not_1_out);
  assign or_2_out = and_1_out | ArithMask;  // OR_Gate or_2, 32 bits wide
  Multiplexer #(.width(32)) multiplexer_5 (.in0(RotOut), .in1(ShiftOut), .out(Out0), .sel(and_2_out));
  and and_3 (and_3_out, InCtl[2], In0[31], not_2_out);
  not not_2 (not_2_out, InCtl[0]);
  MaskGenUni maskgenuni_1 (
    .Shamt({S4_t, S3_t, S2_t, S1_t, S0_t}), .SignBit(In0[31]), .CtlDir(InCtl[0]), .CtlArith(1'b0),
    .Out0(ClearMask));
  MaskGenUni maskgenuni_2 (
    .Shamt({S4_t, S3_t, S2_t, S1_t, S0_t}), .SignBit(In0[31]), .CtlDir(InCtl[0]), .CtlArith(InCtl[2]),
    .Out0(ArithMask));
  Multiplexer #(.width(32)) multiplexer_6 (.in0(and_1_out), .in1(or_2_out), .out(ShiftOut), .sel(and_3_out));
  // Probe on Out0
  // Probe on ShiftOut
  // Probe on ClearMask
  // Probe on ArithMask
  Multiplexer #(.width(32)) multiplexer_7 (
    .in0(multiplexer_4_out), .in1(rot16_32bit_1_out_2), .out(RotOut), .sel(S4_t));
  rot16_32bit rot16_32bit_1 (.in_1(multiplexer_4_out), .out_2(rot16_32bit_1_out_2));
  // Probe on RotOut

  // Other names for the same wires on the sheet: SignBit = In0[31]; Ctl_Dir = InCtl[0]; Ctl_Shift = InCtl[1];
  //   Ctl_Arith = InCtl[2]; ShAmt[4:0] = {S4_t, S3_t, S2_t, S1_t, S0_t}

  // Notes on the sheet:
  //   In0: initial=0xaaaaaaaa
  //   Control Logic
  //   Shift direction logic
  //   Left = Ctl_Dir = 1, Right = Ctl_Dir = 0
  //   Rotate = Ctl_Shift = 1, Shift = Ctl_Shift = 0
  //   Arithmetic Op = Ctl_Arith = 1, Logical Op = Ctl_Arith = 0
  //   apply logical mask, choose OR arithmetic if Shift right Arithmetic
  //   Isolation Mask
  //   Sign Injection
endmodule

module rot16_32bit (
  input  [31:0] in_1,
  output [31:0] out_2
);


  assign out_2 = {in_1[15:0], in_1[31:16]};
endmodule

module rot8_32bit (
  input  [31:0] in_1,
  output [31:0] out_2
);


  assign out_2 = {in_1[7:0], in_1[31:8]};

  // Notes on the sheet:
  //   PUT CIRCUITRY HERE
endmodule

module rot4_32bit (
  input  [31:0] in_1,
  output [31:0] out_2
);


  assign out_2 = {in_1[3:0], in_1[31:4]};
endmodule

module rot2_32bit (
  input  [31:0] in_1,
  output [31:0] out_2
);


  assign out_2 = {in_1[1:0], in_1[31:2]};
endmodule

module rot1_32bit (
  input  [31:0] in_1,
  output [31:0] out_2
);


  assign out_2 = {in_1[0], in_1[31:1]};
endmodule

module ShiftDirCtl (
  input  [4:0] InShAmt,
  input  InDir,
  output [4:0] OutDir
);

  wire [4:0] adder_1_out, not_1_out;

  assign not_1_out = ~InShAmt;  // NOT_Gate not_1, 5 bits wide
  Adder #(.width(5)) adder_1 (.a(not_1_out), .b({5{1'b0}}), .out(adder_1_out), .cin(1'b1));  // open: cout
  Multiplexer #(.width(5)) multiplexer_1 (.in0(InShAmt), .in1(adder_1_out), .out(OutDir), .sel(InDir));

  // Notes on the sheet:
  //   Shift direction logic
  //   If InDir is 1 then take two's compliment
  //   Rotate(X,Y) = Rotate(X, TwosCompliment(Y))
  //   Rotate Left K = Rotate Right 32 - K
endmodule

module MaskGenUni (
  input  [4:0] Shamt,
  input  SignBit,
  input  CtlDir,
  input  CtlArith,
  output [31:0] Out0
);

  wire and_1_out, not_1_out;
  wire [31:0] bit_extender_1_out, multiplexer_1_out, multiplexer_2_out, multiplexer_4_out, multiplexer_5_out,
       multiplexer_6_out, rot1_32bit_1_out_2, rot2_32bit_1_out_2, rot4_32bit_1_out_2, rot8_32bit_1_out_2,
       rot16_32bit_1_out_2, SeedBus, SeedBusInverse;

  rot1_32bit rot1_32bit_1 (.in_1(SeedBusInverse), .out_2(rot1_32bit_1_out_2));
  Multiplexer #(.width(32)) multiplexer_1 (
    .in0(SeedBusInverse), .in1({SeedBus[0], rot1_32bit_1_out_2[31:1]}), .out(multiplexer_1_out),
    .sel(Shamt[0]));
  rot2_32bit rot2_32bit_1 (.in_1(multiplexer_1_out), .out_2(rot2_32bit_1_out_2));
  not not_1 (not_1_out, CtlDir);
  Multiplexer #(.width(32)) multiplexer_2 (.in0({32{1'b0}}), .in1({32{1'b1}}), .out(multiplexer_2_out), .sel(CtlDir));
  assign bit_extender_1_out = {{31{SignBit}}, SignBit};  // Bit_Extender bit_extender_1
  and and_1 (and_1_out, CtlArith, not_1_out);
  // Probe on SeedBus
  Multiplexer #(.width(32)) multiplexer_3 (
    .in0(multiplexer_2_out), .in1(bit_extender_1_out), .out(SeedBus), .sel(and_1_out));
  Multiplexer #(.width(32)) multiplexer_4 (
    .in0(multiplexer_1_out), .in1({SeedBus[1:0], rot2_32bit_1_out_2[29:0]}), .out(multiplexer_4_out),
    .sel(Shamt[1]));
  assign SeedBusInverse = ~SeedBus;  // NOT_Gate not_2, 32 bits wide
  rot4_32bit rot4_32bit_1 (.in_1(multiplexer_4_out), .out_2(rot4_32bit_1_out_2));
  Multiplexer #(.width(32)) multiplexer_5 (
    .in0(multiplexer_4_out), .in1({SeedBus[3:0], rot4_32bit_1_out_2[27:0]}), .out(multiplexer_5_out),
    .sel(Shamt[2]));
  rot8_32bit rot8_32bit_1 (.in_1(multiplexer_5_out), .out_2(rot8_32bit_1_out_2));
  Multiplexer #(.width(32)) multiplexer_6 (
    .in0(multiplexer_5_out), .in1({SeedBus[7:0], rot8_32bit_1_out_2[23:0]}), .out(multiplexer_6_out),
    .sel(Shamt[3]));
  rot16_32bit rot16_32bit_1 (.in_1(multiplexer_6_out), .out_2(rot16_32bit_1_out_2));
  Multiplexer #(.width(32)) multiplexer_7 (
    .in0(multiplexer_6_out), .in1({SeedBus[15:0], rot16_32bit_1_out_2[15:0]}), .out(Out0), .sel(Shamt[4]));

  // Other names for the same wires on the sheet: Ctl_Arith = CtlArith; Ctl_Dir = CtlDir; S0_t = Shamt[0];
  //   S1_t = Shamt[1]; S2_t = Shamt[2]; S3_t = Shamt[3]; S4_t = Shamt[4]

  // Notes on the sheet:
  //   In sign bit, the MSB or of original number
  //   Left = Ctl_Dir = 1, Right = Ctl_Dir = 0
  //   Arithmetic Op = Ctl_Arith = 1, Logical Op = Ctl_Arith = 0
  //   Take seed all ones or all zeros depending on direction
  //   Only choose sign bit if both Arithmetic and right shift
endmodule
