// Logisim project TestHarnessTemplate.circ as structural Verilog: 1 circuit, main circuit TestHarness
module TestHarness (
  output [31:0] Result,
  output Halt
);

  wire clock_1_out, clock_2_out, Halt_t, MemRead, MemWrite, SysClk;
  wire [1:0] AddrOffset;
  wire [3:0] StoreMask;
  wire [31:0] finalInst, Inst, MemOut, MemWriteData, PC;
  wire [31:2] MemAddr;

  // Probe on PC
  ROM #(.addrWidth(10), .dataWidth(32)) IMem (.addr(PC[11:2]), .data(Inst));
  Clock clock_1 (.out(clock_1_out));
  Register #(.width(1)) register_1 (.D(1'b1), .en(Halt_t), .clk(clock_2_out), .Q(Halt));  // open: clr
  Clock clock_2 (.out(clock_2_out));
  RiskVCPU riskvcpu_1 (
    .SysClk(SysClk), .EXT_CTL_EN(1'b1), .Inst(Inst), .MemOutData(MemOut), .HALT(Halt), .IMemPC(PC),
    .DMemAddr({MemAddr, AddrOffset}), .DMemWE(MemWrite), .DMemRead(MemRead), .DMemMask(StoreMask),
    .DMemWriteData(MemWriteData), .TEST_Out(Result));
  and and_1 (SysClk, clock_1_out, ~Halt);  // AND_Gate
  // Probe on Inst
  Adder #(.width(32)) adder_1 (.a(32'hcc), .b(32'h8), .out(finalInst));  // open: cin, cout
  Comparator #(.width(32)) comparator_1 (.a(PC), .b(finalInst), .eq(Halt_t));  // open: gt, lt
  // Probe on {MemAddr, AddrOffset}
  // Probe on MemWriteData
  RAM #(.addrWidth(10), .asyncread("true"), .byteenables("byteEnables"), .dataWidth(32)) ram_1 (
    .addr(MemAddr[11:2]), .we(MemWrite), .oe(MemRead), .clk(SysClk), .din(MemWriteData), .dout(MemOut),
    .be3(StoreMask[3]), .be2(StoreMask[2]), .be1(StoreMask[1]), .be0(StoreMask[0]));
  // Probe on MemOut

  // Other names for the same wires on the sheet: Halted = Halt; MemAddr[1:0] = AddrOffset;
  //   x31TestResult[31:0] = Result

  // Notes on the sheet:
  //   contents of IMem (hex, n*v repeats v):
  //   b7 137 1b7 237 fb7 2537 1597 f00093 140a113 a0b193 fff0c213 10e293 10f313 209393 10d413 40125493
  //   708633 401386b3 609733 c2a7b3 563833 50c8b3 63d933 406259b3 60ea33 60fab3 4000b13 abcdebb7 4f0b8b93
  //   17b2023 b2c03 508463 480006f 709463 400006f 72c463 380006f 53d463 300006f 72e463 280006f 53f463
  //   200006f c00eef ce8067 140006f ff9ff06f 0 100f93 80006f fff00f93 6f
  //   Set last address --->
  //   TEST_LABEL
  //   Last Instruction Addr
  //   MEM - Memory
endmodule
