// Logisim project test_align.circ as structural Verilog: 1 circuit, main circuit TestHarness
module TestHarness (
  output [31:0] Result,
  output halt
);

  wire clock_1_out, clock_2_out, Halt_t, MemRead, MemWrite, SysClk;
  wire [1:0] AddrOffset;
  wire [3:0] StoreMask;
  wire [31:0] finalInst, Inst, MemOut, MemWriteData, PC;
  wire [31:2] MemAddr;

  // Probe on PC
  ROM #(.addrWidth(10), .dataWidth(32)) IMem (.addr(PC[11:2]), .data(Inst));
  Clock clock_1 (.out(clock_1_out));
  and and_1 (SysClk, clock_1_out, ~halt);  // AND_Gate
  Register #(.width(1)) register_1 (.D(1'b1), .en(Halt_t), .clk(clock_2_out), .Q(halt));  // open: clr
  Clock clock_2 (.out(clock_2_out));
  RiskVCPU riskvcpu_1 (
    .SysClk(SysClk), .EXT_CTL_EN(1'b1), .Inst(Inst), .MemOutData(MemOut), .HALT(halt), .IMemPC(PC),
    .DMemAddr({MemAddr, AddrOffset}), .DMemWE(MemWrite), .DMemRead(MemRead), .DMemMask(StoreMask),
    .DMemWriteData(MemWriteData), .TEST_Out(Result));
  // Probe on Inst
  Adder #(.width(32)) adder_1 (.a(32'h144), .b(32'h8), .out(finalInst));  // open: cin, cout
  Comparator #(.width(32)) comparator_1 (.a(PC), .b(finalInst), .eq(Halt_t));  // open: gt, lt
  // Probe on {MemAddr, AddrOffset}
  // Probe on MemWriteData
  RAM #(.addrWidth(10), .asyncread("true"), .byteenables("byteEnables"), .dataWidth(32)) ram_1 (
    .addr(MemAddr[11:2]), .we(MemWrite), .oe(MemRead), .clk(SysClk), .din(MemWriteData), .dout(MemOut),
    .be3(StoreMask[3]), .be2(StoreMask[2]), .be1(StoreMask[1]), .be0(StoreMask[0]));
  // Probe on MemOut

  // Other names for the same wires on the sheet: Halted = halt; MemAddr[1:0] = AddrOffset;
  //   x31TestResult[31:0] = Result

  // Notes on the sheet:
  //   contents of IMem (hex, n*v repeats v):
  //   fb7 deadc137 eef10113 ff00193 55555237 55520213 4000293 128313 228393 328413 8000493 7f00c93 22a023
  //   2a503 10251463 328023 28583 fff00f13 fe59c63 2c603 e361863 430023 30683 5500f13 fe69063 338023 38703
  //   fff00f13 de71863 440023 44783 5500f13 de79063 2a803 ff560f37 f55f0f13 be81863 22a023 429023 29883
  //   5f37 555f0f13 9e89c63 239023 39903 ffffcf37 eeff0f13 9e91263 3d983 cf37 eeff0f13 7e99a63 22a023
  //   431023 30a83 5500f13 7ea9063 38b03 5eb1c63 31b83 5f37 555f0f13 5eb9463 2ac03 de555f37 5eff0f13
  //   3ec1c63 22a023 9300a3 38d03 f8000f13 3ed1263 19300a3 38d83 19d9c63 432023 2ae03 4e1663 100f93 80006f
  //   fff00f93 6f
  //   test_align
  //   Last Instruction Addr
  //   MEM - Memory
endmodule
