// Logisim project test_branch.circ as structural Verilog: 1 circuit, main circuit TestHarness
module TestHarness (
  output [31:0] Result,
  output halt
);

  wire clock_1_out, clock_2_out, Halt_t, MemRead, MemWrite, SysClk;
  wire [1:0] AddrOffset;
  wire [3:0] StoreMask;
  wire [31:0] finalInst, Inst, MemOut, MemWriteData, PC;
  wire [31:2] MemAddr;

  // Probe on PC
  ROM #(.addrWidth(10), .dataWidth(32)) IMem (.addr(PC[11:2]), .data(Inst));
  Clock clock_1 (.out(clock_1_out));
  and and_1 (SysClk, clock_1_out, ~halt);  // AND_Gate
  Register #(.width(1)) register_1 (.D(1'b1), .en(Halt_t), .clk(clock_2_out), .Q(halt));  // open: clr
  Clock clock_2 (.out(clock_2_out));
  RiskVCPU riskvcpu_1 (
    .SysClk(SysClk), .EXT_CTL_EN(1'b1), .Inst(Inst), .MemOutData(MemOut), .HALT(halt), .IMemPC(PC),
    .DMemAddr({MemAddr, AddrOffset}), .DMemWE(MemWrite), .DMemRead(MemRead), .DMemMask(StoreMask),
    .DMemWriteData(MemWriteData), .TEST_Out(Result));
  // Probe on Inst
  Adder #(.width(32)) adder_1 (.a(32'h68), .b(32'h8), .out(finalInst));  // open: cin, cout
  Comparator #(.width(32)) comparator_1 (.a(PC), .b(finalInst), .eq(Halt_t));  // open: gt, lt
  // Probe on {MemAddr, AddrOffset}
  // Probe on MemWriteData
  RAM #(.addrWidth(10), .asyncread("true"), .byteenables("byteEnables"), .dataWidth(32)) ram_1 (
    .addr(MemAddr[11:2]), .we(MemWrite), .oe(MemRead), .clk(SysClk), .din(MemWriteData), .dout(MemOut),
    .be3(StoreMask[3]), .be2(StoreMask[2]), .be1(StoreMask[1]), .be0(StoreMask[0]));
  // Probe on MemOut

  // Other names for the same wires on the sheet: Halted = halt; MemAddr[1:0] = AddrOffset;
  //   x31TestResult[31:0] = Result

  // Notes on the sheet:
  //   contents of IMem (hex, n*v repeats v):
  //   93 113 193 213 293 f93 8000093 fff00113 20a023 a183 2219e63 6400213 c800293 42a333 2031663 f24393
  //   6b00f13 3e39063 521663 fff00f93 180006f 0 0 100f93 80006f fff00f93 6f
  //   test_branch
  //   Last Instruction Addr
  //   MEM - Memory
endmodule
