// Logisim project test_byte.circ as structural Verilog: 1 circuit, main circuit TestHarness
module TestHarness (
  output [31:0] Result,
  output halt
);

  wire clock_1_out, clock_2_out, Halt_t, MemRead, MemWrite, SysClk;
  wire [1:0] AddrOffset;
  wire [3:0] StoreMask;
  wire [31:0] finalInst, Inst, MemOut, MemWriteData, PC;
  wire [31:2] MemAddr;

  // Probe on PC
  ROM #(.addrWidth(10), .dataWidth(32)) IMem (.addr(PC[11:2]), .data(Inst));
  Clock clock_1 (.out(clock_1_out));
  and and_1 (SysClk, clock_1_out, ~halt);  // AND_Gate
  Register #(.width(1)) register_1 (.D(1'b1), .en(Halt_t), .clk(clock_2_out), .Q(halt));  // open: clr
  Clock clock_2 (.out(clock_2_out));
  RiskVCPU riskvcpu_1 (
    .SysClk(SysClk), .EXT_CTL_EN(1'b1), .Inst(Inst), .MemOutData(MemOut), .HALT(halt), .IMemPC(PC),
    .DMemAddr({MemAddr, AddrOffset}), .DMemWE(MemWrite), .DMemRead(MemRead), .DMemMask(StoreMask),
    .DMemWriteData(MemWriteData), .TEST_Out(Result));
  // Probe on Inst
  Adder #(.width(32)) adder_1 (.a(32'hc4), .b(32'h8), .out(finalInst));  // open: cin, cout
  Comparator #(.width(32)) comparator_1 (.a(PC), .b(finalInst), .eq(Halt_t));  // open: gt, lt
  // Probe on {MemAddr, AddrOffset}
  // Probe on MemWriteData
  RAM #(.addrWidth(10), .asyncread("true"), .byteenables("byteEnables"), .dataWidth(32)) ram_1 (
    .addr(MemAddr[11:2]), .we(MemWrite), .oe(MemRead), .clk(SysClk), .din(MemWriteData), .dout(MemOut),
    .be3(StoreMask[3]), .be2(StoreMask[2]), .be1(StoreMask[1]), .be0(StoreMask[0]));
  // Probe on MemOut

  // Other names for the same wires on the sheet: Halted = halt; MemAddr[1:0] = AddrOffset;
  //   x31TestResult[31:0] = Result

  // Notes on the sheet:
  //   contents of IMem (hex, n*v repeats v):
  //   fb7 4000293 7ff00313 130313 deadc137 eef10113 22a023 628023 28503 8051e63 2280a3 128583 fef00f13
  //   9e59663 12c603 ef00f13 9e61063 22a023 229023 29683 ffffcf37 eeff0f13 7e69463 22a023 229123 229703
  //   5e71c63 22d783 cf37 eeff0f13 5e79463 22a023 2290a3 128803 fbe00f13 3e81a63 228883 fef00f13 3e89463
  //   129903 ffffcf37 eeff0f13 1e91c63 22a023 2aa03 2a1663 100f93 80006f fff00f93 6f
  //   test_byte
  //   Last Instruction Addr
  //   MEM - Memory
endmodule
