// Logisim project test_csr.circ as structural Verilog: 1 circuit, main circuit TestHarness
module TestHarness (
  output halt,
  output [31:0] Result,
  output [31:0] InstRetCount
);

  wire clock_1_out, clock_2_out, Halt_t, MemRead, MemWrite, SysClk;
  wire [1:0] AddrOffset;
  wire [3:0] StoreMask;
  wire [31:0] finalInst, HALT_EXT, Inst, MemOut, MemWriteData, PC, TestInstRet, TestResult;
  wire [31:2] MemAddr;

  // Probe on PC
  ROM #(.addrWidth(10), .dataWidth(32)) IMem (.addr(PC[11:2]), .data(Inst));
  Clock clock_1 (.out(clock_1_out));
  Register #(.width(1)) register_1 (.D(1'b1), .en(Halt_t), .clk(clock_2_out), .Q(halt));  // open: clr
  Clock clock_2 (.out(clock_2_out));
  // RiskVCPU riskvcpu_1: pin names not known; wires that end beside it: SysClk, 1'b1, Inst, MemOut, halt, PC, {MemAddr, AddrOffset}, MemWrite, MemRead, StoreMask, MemWriteData, TestResult, TestInstRet
  and and_1 (SysClk, clock_1_out, ~halt);  // AND_Gate
  // Probe on Inst
  Adder #(.width(32)) adder_1 (.a(32'hc0), .b(32'h8), .out(finalInst));  // open: cin, cout
  Comparator #(.width(32)) comparator_1 (.a(PC), .b(finalInst), .eq(Halt_t));  // open: gt, lt
  assign HALT_EXT = {{31{halt}}, halt};  // Bit_Extender bit_extender_1
  // Probe on {MemAddr, AddrOffset}
  // Probe on MemWriteData
  RAM #(.addrWidth(10), .asyncread("true"), .byteenables("byteEnables"), .dataWidth(32)) ram_1 (
    .addr(MemAddr[11:2]), .we(MemWrite), .oe(MemRead), .clk(SysClk), .din(MemWriteData), .dout(MemOut),
    .be3(StoreMask[3]), .be2(StoreMask[2]), .be1(StoreMask[1]), .be0(StoreMask[0]));
  assign Result = TestResult & HALT_EXT;  // AND_Gate and_2, 32 bits wide
  // Probe on MemOut
  assign InstRetCount = TestInstRet & HALT_EXT;  // AND_Gate and_3, 32 bits wide

  // Other names for the same wires on the sheet: Halted = halt; MemAddr[1:0] = AddrOffset

  // Notes on the sheet:
  //   contents of IMem (hex, n*v repeats v):
  //   ff00093 f00113 193 100213 7c0091f3 a019263 7c0131f3 8119e63 7c0021f3 f000293 8519863 7c12d1f3
  //   8019463 7c1861f3 500293 6519e63 7c10f1f3 1500293 6519863 7c1021f3 1400293 6519263 c00020f3 13 13 13
  //   c0002173 20a1b3 4419463 c02020f3 100293 200293 c0202173 401101b3 200293 2519663 7c0021f3 f000293
  //   2519063 7c0071f3 519c63 7c0021f3 519863 40006f 7c00d073 c0006f 7c015073 40006f 6f
  //   Set last address --->
  //   TEST_LABEL
  //   Last Instruction Addr
  //   MEM - Memory
endmodule
