// Logisim project test_pipeline.circ as structural Verilog: 1 circuit, main circuit TestHarness
module TestHarness (
  output [31:0] Result,
  output Halt
);

  wire clock_1_out, clock_2_out, Halt_t, MemRead, MemWrite, SysClk;
  wire [1:0] AddrOffset;
  wire [3:0] StoreMask;
  wire [31:0] finalInst, Inst, MemOut, MemWriteData, PC;
  wire [31:2] MemAddr;

  // Probe on PC
  ROM #(.addrWidth(10), .dataWidth(32)) IMem (.addr(PC[11:2]), .data(Inst));
  Clock clock_1 (.out(clock_1_out));
  Register #(.width(1)) register_1 (.D(1'b1), .en(Halt_t), .clk(clock_2_out), .Q(Halt));  // open: clr
  Clock clock_2 (.out(clock_2_out));
  RiskVCPU riskvcpu_1 (
    .SysClk(SysClk), .EXT_CTL_EN(1'b1), .Inst(Inst), .MemOutData(MemOut), .HALT(Halt), .IMemPC(PC),
    .DMemAddr({MemAddr, AddrOffset}), .DMemWE(MemWrite), .DMemRead(MemRead), .DMemMask(StoreMask),
    .DMemWriteData(MemWriteData), .TEST_Out(Result));  // open: TEST_instret
  and and_1 (SysClk, clock_1_out, ~Halt);  // AND_Gate
  // Probe on Inst
  Adder #(.width(32)) adder_1 (.a(32'hb4), .b(32'h8), .out(finalInst));  // open: cin, cout
  Comparator #(.width(32)) comparator_1 (.a(PC), .b(finalInst), .eq(Halt_t));  // open: gt, lt
  // Probe on {MemAddr, AddrOffset}
  // Probe on MemWriteData
  RAM #(.addrWidth(10), .asyncread("true"), .byteenables("byteEnables"), .dataWidth(32)) ram_1 (
    .addr(MemAddr[11:2]), .we(MemWrite), .oe(MemRead), .clk(SysClk), .din(MemWriteData), .dout(MemOut),
    .be3(StoreMask[3]), .be2(StoreMask[2]), .be1(StoreMask[1]), .be0(StoreMask[0]));
  // Probe on MemOut

  // Other names for the same wires on the sheet: Halted = Halt; MemAddr[1:0] = AddrOffset;
  //   x31TestResult[31:0] = Result

  // Notes on the sheet:
  //   contents of IMem (hex, n*v repeats v):
  //   b7 137 1b7 237 fb7 f00093 108133 ff610193 1400213 418463 880006f 6400293 313 5283b3 c800413 838463
  //   700006f 4000493 2a00513 a4a023 4a583 858613 3200693 d60463 500006f 8000713 6300793 178813 1072023
  //   72883 6400913 1288463 300006f 1f400993 19000a13 64a0a93 1598463 1c0006f b17 10b0b13 b0be7 c0006f
  //   100f93 80006f fff00f93 6f
  //   Set last address --->
  //   test_pipeline
  //   Last Instruction Addr
  //   MEM - Memory
endmodule
